// Logisim project 16进制序列匹配.circ as structural Verilog: 1 circuit, main circuit main
module main (
  input  [3:0] \input ,
  input  reset,
  input  clk,
  output [1:0] \output 
);

  wire comparator_1_eq, comparator_2_eq, comparator_3_eq;
  wire [11:0] multiplexer_1_out, multiplexer_2_out, now, shifter_1_out;
  wire [11:2] multiplexer_3_out;

  Comparator #(.width(12), .mode("unsigned")) comparator_1 (.a(now), .b(12'ha0), .eq(comparator_1_eq));  // open: gt, lt
  Shifter #(.width(12)) shifter_1 (.in(now), .\dist (4'b0100), .out(shifter_1_out));
  Multiplexer #(.width(12)) multiplexer_1 (
    .in0({12{1'b0}}), .in1(12'h3), .out(multiplexer_1_out), .sel(comparator_1_eq));  // open: en
  Comparator #(.width(12), .mode("unsigned")) comparator_2 (
    .a(now), .b(12'ha0e), .eq(comparator_2_eq));  // open: gt, lt
  Multiplexer #(.width(12)) multiplexer_2 (
    .in0(multiplexer_1_out), .in1(12'h2), .out(multiplexer_2_out), .sel(comparator_2_eq));  // open: en
  Comparator #(.width(12), .mode("unsigned")) comparator_3 (
    .a(now), .b(12'heee), .eq(comparator_3_eq));  // open: gt, lt
  Register #(.width(12)) register_1 (.D({shifter_1_out[11:4], \input }), .Q(now), .clk(clk), .clr(reset));  // open: en
  Multiplexer #(.width(12)) multiplexer_3 (
    .in0(multiplexer_2_out), .in1(12'h1), .out({multiplexer_3_out, \output }), .sel(comparator_3_eq));  // open: en

  // Other names for the same wires on the sheet: IN[3:0] = \input ; RST = reset
endmodule
