// Logisim project 未出现的最小正整数.circ as structural Verilog: 1 circuit, main circuit main
module main (
  input  [4:0] in_1,
  input  [4:0] in_2,
  input  [4:0] in_3,
  input  [4:0] in_4,
  input  [4:0] in_5,
  output [4:0] out_6
);

  wire comparator_1_eq, comparator_2_eq, comparator_3_eq, comparator_4_eq, comparator_5_eq, comparator_6_eq,
       comparator_7_eq, comparator_8_eq, comparator_9_eq, comparator_10_eq, comparator_11_eq,
       comparator_12_eq, comparator_13_eq, comparator_14_eq, comparator_15_eq, comparator_16_eq,
       comparator_17_eq, comparator_18_eq, comparator_19_eq, comparator_20_eq, comparator_21_eq,
       comparator_22_eq, comparator_23_eq, comparator_24_eq, comparator_25_eq, comparator_26_eq,
       comparator_27_eq, comparator_28_eq, comparator_29_eq, comparator_30_eq, e1, e2, e3, e4, e5, e6;
  wire [4:0] multiplexer_1_out, multiplexer_2_out, multiplexer_3_out, multiplexer_4_out;

  Comparator #(.width(5), .mode("unsigned")) comparator_1 (
    .a(in_1), .b(5'b00001), .eq(comparator_1_eq));  // open: gt, lt
  Comparator #(.width(5), .mode("unsigned")) comparator_2 (
    .a(in_2), .b(5'b00001), .eq(comparator_2_eq));  // open: gt, lt
  Comparator #(.width(5), .mode("unsigned")) comparator_3 (
    .a(in_3), .b(5'b00001), .eq(comparator_3_eq));  // open: gt, lt
  Comparator #(.width(5), .mode("unsigned")) comparator_4 (
    .a(in_4), .b(5'b00001), .eq(comparator_4_eq));  // open: gt, lt
  Comparator #(.width(5), .mode("unsigned")) comparator_5 (
    .a(in_5), .b(5'b00001), .eq(comparator_5_eq));  // open: gt, lt
  Comparator #(.width(5), .mode("unsigned")) comparator_6 (
    .a(in_1), .b(5'b00010), .eq(comparator_6_eq));  // open: gt, lt
  Comparator #(.width(5), .mode("unsigned")) comparator_7 (
    .a(in_2), .b(5'b00010), .eq(comparator_7_eq));  // open: gt, lt
  Comparator #(.width(5), .mode("unsigned")) comparator_8 (
    .a(in_3), .b(5'b00010), .eq(comparator_8_eq));  // open: gt, lt
  Comparator #(.width(5), .mode("unsigned")) comparator_9 (
    .a(in_4), .b(5'b00010), .eq(comparator_9_eq));  // open: gt, lt
  Comparator #(.width(5), .mode("unsigned")) comparator_10 (
    .a(in_5), .b(5'b00010), .eq(comparator_10_eq));  // open: gt, lt
  or or_1 (e1, comparator_1_eq, comparator_2_eq, comparator_3_eq, comparator_4_eq, comparator_5_eq);
  or or_2 (e2, comparator_6_eq, comparator_7_eq, comparator_8_eq, comparator_9_eq, comparator_10_eq);
  Multiplexer #(.width(5)) multiplexer_1 (
    .in0(5'b00100), .in1(multiplexer_2_out), .out(multiplexer_1_out), .sel(e4));  // open: en
  Multiplexer #(.width(5)) multiplexer_2 (
    .in0(5'b00101), .in1(5'b00110), .out(multiplexer_2_out), .sel(e5));  // open: en
  Comparator #(.width(5), .mode("unsigned")) comparator_11 (
    .a(in_1), .b(5'b00011), .eq(comparator_11_eq));  // open: gt, lt
  Comparator #(.width(5), .mode("unsigned")) comparator_12 (
    .a(in_2), .b(5'b00011), .eq(comparator_12_eq));  // open: gt, lt
  Comparator #(.width(5), .mode("unsigned")) comparator_13 (
    .a(in_3), .b(5'b00011), .eq(comparator_13_eq));  // open: gt, lt
  Comparator #(.width(5), .mode("unsigned")) comparator_14 (
    .a(in_4), .b(5'b00011), .eq(comparator_14_eq));  // open: gt, lt
  Comparator #(.width(5), .mode("unsigned")) comparator_15 (
    .a(in_5), .b(5'b00011), .eq(comparator_15_eq));  // open: gt, lt
  Comparator #(.width(5), .mode("unsigned")) comparator_16 (
    .a(in_1), .b(5'b00100), .eq(comparator_16_eq));  // open: gt, lt
  Comparator #(.width(5), .mode("unsigned")) comparator_17 (
    .a(in_2), .b(5'b00100), .eq(comparator_17_eq));  // open: gt, lt
  Comparator #(.width(5), .mode("unsigned")) comparator_18 (
    .a(in_3), .b(5'b00100), .eq(comparator_18_eq));  // open: gt, lt
  Comparator #(.width(5), .mode("unsigned")) comparator_19 (
    .a(in_4), .b(5'b00100), .eq(comparator_19_eq));  // open: gt, lt
  Comparator #(.width(5), .mode("unsigned")) comparator_20 (
    .a(in_5), .b(5'b00100), .eq(comparator_20_eq));  // open: gt, lt
  Multiplexer #(.width(5)) multiplexer_3 (
    .in0(5'b00010), .in1(multiplexer_4_out), .out(multiplexer_3_out), .sel(e2));  // open: en
  Multiplexer #(.width(5)) multiplexer_4 (
    .in0(5'b00011), .in1(multiplexer_1_out), .out(multiplexer_4_out), .sel(e3));  // open: en
  or or_3 (e3, comparator_11_eq, comparator_12_eq, comparator_13_eq, comparator_14_eq, comparator_15_eq);
  or or_4 (e4, comparator_16_eq, comparator_17_eq, comparator_18_eq, comparator_19_eq, comparator_20_eq);
  Multiplexer #(.width(5)) multiplexer_5 (.in0(5'b00001), .in1(multiplexer_3_out), .out(out_6), .sel(e1));  // open: en
  Comparator #(.width(5), .mode("unsigned")) comparator_21 (
    .a(in_1), .b(5'b00101), .eq(comparator_21_eq));  // open: gt, lt
  Comparator #(.width(5), .mode("unsigned")) comparator_22 (
    .a(in_2), .b(5'b00101), .eq(comparator_22_eq));  // open: gt, lt
  Comparator #(.width(5), .mode("unsigned")) comparator_23 (
    .a(in_3), .b(5'b00101), .eq(comparator_23_eq));  // open: gt, lt
  Comparator #(.width(5), .mode("unsigned")) comparator_24 (
    .a(in_4), .b(5'b00101), .eq(comparator_24_eq));  // open: gt, lt
  Comparator #(.width(5), .mode("unsigned")) comparator_25 (
    .a(in_5), .b(5'b00101), .eq(comparator_25_eq));  // open: gt, lt
  Comparator #(.width(5), .mode("unsigned")) comparator_26 (
    .a(in_1), .b(5'b00110), .eq(comparator_26_eq));  // open: gt, lt
  Comparator #(.width(5), .mode("unsigned")) comparator_27 (
    .a(in_2), .b(5'b00110), .eq(comparator_27_eq));  // open: gt, lt
  Comparator #(.width(5), .mode("unsigned")) comparator_28 (
    .a(in_3), .b(5'b00110), .eq(comparator_28_eq));  // open: gt, lt
  Comparator #(.width(5), .mode("unsigned")) comparator_29 (
    .a(in_4), .b(5'b00110), .eq(comparator_29_eq));  // open: gt, lt
  Comparator #(.width(5), .mode("unsigned")) comparator_30 (
    .a(in_5), .b(5'b00110), .eq(comparator_30_eq));  // open: gt, lt
  or or_5 (e5, comparator_21_eq, comparator_22_eq, comparator_23_eq, comparator_24_eq, comparator_25_eq);
  or or_6 (e6, comparator_26_eq, comparator_27_eq, comparator_28_eq, comparator_29_eq, comparator_30_eq);

  // Other names for the same wires on the sheet: in1[4:0] = in_1; in2[4:0] = in_2; in3[4:0] = in_3; in4[4:0] = in_4;
  //   in5[4:0] = in_5
endmodule
