// Logisim project P0_L0_CRC.circ as structural Verilog: 2 circuits, main circuit CRC
module CRC (
  input  [7:0] in_1,
  input  [3:0] in_2,
  output [10:0] out_3
);

  wire [2:0] \四位模二除法器_1_余数 , \四位模二除法器_2_余数 , \四位模二除法器_3_余数 , \四位模二除法器_4_余数 , \四位模二除法器_5_余数 , \四位模二除法器_6_余数 ,
       \四位模二除法器_7_余数 ;

  \四位模二除法器  \u_四位模二除法器_1  (.\被除数 (in_1[7:4]), .\除数 (in_2), .\余数 (\四位模二除法器_1_余数 ));  // open: 商
  // Probe on \四位模二除法器_1_余数 
  \四位模二除法器  \u_四位模二除法器_2  (.\被除数 ({\四位模二除法器_1_余数 , in_1[3]}), .\除数 (in_2), .\余数 (\四位模二除法器_2_余数 ));  // open: 商
  // Probe on \四位模二除法器_2_余数 
  \四位模二除法器  \u_四位模二除法器_3  (.\被除数 ({\四位模二除法器_2_余数 , in_1[2]}), .\除数 (in_2), .\余数 (\四位模二除法器_3_余数 ));  // open: 商
  // Probe on \四位模二除法器_3_余数 
  \四位模二除法器  \u_四位模二除法器_4  (.\被除数 ({\四位模二除法器_3_余数 , in_1[1]}), .\除数 (in_2), .\余数 (\四位模二除法器_4_余数 ));  // open: 商
  // Probe on \四位模二除法器_4_余数 
  \四位模二除法器  \u_四位模二除法器_5  (.\被除数 ({\四位模二除法器_4_余数 , in_1[0]}), .\除数 (in_2), .\余数 (\四位模二除法器_5_余数 ));  // open: 商
  // Probe on \四位模二除法器_5_余数 
  \四位模二除法器  \u_四位模二除法器_6  (.\被除数 ({\四位模二除法器_5_余数 , 1'b0}), .\除数 (in_2), .\余数 (\四位模二除法器_6_余数 ));  // open: 商
  \四位模二除法器  \u_四位模二除法器_7  (.\被除数 ({\四位模二除法器_6_余数 , 1'b0}), .\除数 (in_2), .\余数 (\四位模二除法器_7_余数 ));  // open: 商
  // Probe on \四位模二除法器_6_余数 
  \四位模二除法器  \u_四位模二除法器_8  (.\被除数 ({\四位模二除法器_7_余数 , 1'b0}), .\除数 (in_2), .\余数 (out_3[2:0]));  // open: 商
  // Probe on \四位模二除法器_7_余数 

  assign out_3[10:3] = in_1;

  // Other names for the same wires on the sheet: 原数据帧[7:0] = in_1; 除数[3:0] = in_2
endmodule

module \四位模二除法器  (
  input  [3:0] \被除数 ,
  input  [3:0] \除数 ,
  output \商 ,
  output [2:0] \余数 
);

  wire [3:0] xor_1_out;

  assign xor_1_out = \被除数  ^ \除数 ;  // XOR_Gate xor_1, 4 bits wide
  Multiplexer multiplexer_1 (.in0(1'b0), .in1(1'b1), .out(\商 ), .sel(\被除数 [3]));  // open: en
  Multiplexer #(.width(3)) multiplexer_2 (
    .in0(\被除数 [2:0]), .in1(xor_1_out[2:0]), .out(\余数 ), .sel(\被除数 [3]));  // open: en
endmodule
