// Logisim project P0_L0_FSM.circ as structural Verilog: 4 circuits, main circuit fsm
module fsm (
  input  CLR,
  input  [1:0] In,
  output Z
);

  wire clock_1_out;
  wire [2:0] \状态存储_1_state , \状态转移2_1_next_state ;

  Clock clock_1 (.out(clock_1_out));
  \状态转移2  \u_状态转移2_1  (.state(\状态存储_1_state ), .in(In), .next_state(\状态转移2_1_next_state ));
  \状态存储  \u_状态存储_1  (.next_state(\状态转移2_1_next_state ), .rst(CLR), .clk(clock_1_out), .state(\状态存储_1_state ));
  \状态输出  \u_状态输出_1  (.state(\状态存储_1_state ), .in(In), .out(Z));
endmodule

module \状态存储  (
  input  [2:0] next_state,
  input  rst,
  input  clk,
  output [2:0] state
);

  wire [2:0] multiplexer_1_out;

  Multiplexer #(.width(3)) multiplexer_1 (
    .in0(next_state), .in1(3'b000), .out(multiplexer_1_out), .sel(rst));  // open: en
  Register #(.width(3)) register_1 (.D(multiplexer_1_out), .Q(state), .clk(clk));  // open: en, clr
endmodule

module \状态输出  (
  input  [2:0] state,
  input  [1:0] in,
  output out
);

  wire comparator_1_eq, comparator_2_eq, comparator_3_eq, or_1_out;

  Comparator #(.width(3), .mode("unsigned")) comparator_1 (
    .a(state), .b(3'b011), .eq(comparator_1_eq));  // open: gt, lt
  Comparator #(.width(2), .mode("unsigned")) comparator_2 (.a(in), .b(2'b00), .eq(comparator_2_eq));  // open: gt, lt
  or or_1 (or_1_out, comparator_2_eq, comparator_3_eq);
  Comparator #(.width(2), .mode("unsigned")) comparator_3 (.a(in), .b(2'b10), .eq(comparator_3_eq));  // open: gt, lt
  and and_1 (out, comparator_1_eq, or_1_out);
endmodule

module \状态转移2  (
  input  [2:0] state,
  input  [1:0] in,
  output [2:0] next_state
);

  wire and_2_out, and_3_out, and_4_out, and_5_out, and_6_out, and_7_out, and_8_out, and_9_out, not_1_out,
       not_2_out, not_3_out, not_4_out, not_5_out, not_6_out, not_7_out, not_8_out, not_9_out, not_10_out,
       not_11_out, not_12_out, not_13_out, not_14_out, not_15_out, not_16_out, not_17_out;

  not not_1 (not_1_out, in[0]);
  not not_2 (not_2_out, state[1]);
  not not_3 (not_3_out, in[1]);
  not not_4 (not_4_out, state[1]);
  not not_5 (not_5_out, in[0]);
  not not_6 (not_6_out, state[0]);
  not not_7 (not_7_out, in[1]);
  not not_8 (not_8_out, state[0]);
  not not_9 (not_9_out, in[0]);
  not not_10 (not_10_out, state[1]);
  not not_11 (not_11_out, state[0]);
  not not_12 (not_12_out, in[1]);
  not not_13 (not_13_out, state[1]);
  not not_14 (not_14_out, in[0]);
  not not_15 (not_15_out, state[0]);
  not not_16 (not_16_out, in[0]);
  not not_17 (not_17_out, in[1]);
  and and_1 (next_state[2], state[1], state[0], not_1_out);
  and and_2 (and_2_out, not_2_out, state[0], not_3_out);
  and and_3 (and_3_out, not_4_out, state[0], not_5_out);
  and and_4 (and_4_out, state[1], not_6_out, not_7_out);
  and and_5 (and_5_out, state[1], not_8_out, not_9_out);
  and and_6 (and_6_out, not_10_out, not_11_out, not_12_out, in[0]);
  and and_7 (and_7_out, not_13_out, state[0], not_14_out);
  and and_8 (and_8_out, state[1], not_15_out, not_16_out);
  and and_9 (and_9_out, state[1], state[0], not_17_out, in[0]);
  or or_1 (next_state[1], and_2_out, and_3_out, and_4_out, and_5_out);
  or or_2 (next_state[0], and_6_out, and_7_out, and_8_out, and_9_out);
endmodule
