// Logisim project P0_L0_GRF.circ as structural Verilog: 2 circuits, main circuit grf
module grf (
  input  clk,
  input  reset,
  input  WE,
  input  [4:0] A1,
  input  [4:0] A2,
  input  [4:0] A3,
  input  [31:0] WD,
  output [31:0] RD1,
  output [31:0] RD2
);

  wire and_1_out, and_2_out, and_3_out, and_4_out, and_5_out, and_6_out, and_7_out, and_8_out, and_9_out,
       and_10_out, and_11_out, and_12_out, and_13_out, and_14_out, and_15_out, and_16_out, and_17_out,
       and_18_out, and_19_out, and_20_out, and_21_out, and_22_out, and_23_out, and_24_out, and_25_out,
       and_26_out, and_27_out, and_28_out, and_29_out, and_30_out, and_31_out, and_32_out, WE0, WE1, WE2,
       WE3, WE4, WE5, WE6, WE7, WE8, WE9, WE10, WE11, WE12, WE13, WE14, WE15, WE16, WE17, WE18, WE19, WE20,
       WE21, WE22, WE23, WE24, WE25, WE26, WE27, WE28, WE29, WE30, WE31;
  wire [31:0] D0, D1, D2, D3, D4, D5, D6, D7, D8, D9, D10, D11, D12, D13, D14, D15, D16, D17, D18, D19, D20,
       D21, D22, D23, D24, D25, D26, D27, D28, D29, D30, D31;

  Decoder #(.select(5)) decoder_1 (
    .out0(WE0), .out1(WE1), .out2(WE2), .out3(WE3), .out4(WE4), .out5(WE5), .out6(WE6), .out7(WE7),
    .out8(WE8), .out9(WE9), .out10(WE10), .out11(WE11), .out12(WE12), .out13(WE13), .out14(WE14),
    .out15(WE15), .out16(WE16), .out17(WE17), .out18(WE18), .out19(WE19), .out20(WE20), .out21(WE21),
    .out22(WE22), .out23(WE23), .out24(WE24), .out25(WE25), .out26(WE26), .out27(WE27), .out28(WE28),
    .out29(WE29), .out30(WE30), .out31(WE31), .sel(A3));  // open: en
  and and_1 (and_1_out, WE, WE0);
  and and_2 (and_2_out, WE, WE1);
  and and_3 (and_3_out, WE, WE2);
  and and_4 (and_4_out, WE, WE3);
  and and_5 (and_5_out, WE, WE4);
  and and_6 (and_6_out, WE, WE5);
  and and_7 (and_7_out, WE, WE6);
  and and_8 (and_8_out, WE, WE7);
  \_32位带使能异步复位寄存器  \u_32位带使能异步复位寄存器_1  (.CLK(clk), .RESET(reset), .EN(and_1_out), .D({32{1'b0}}), .Q(D0));
  \_32位带使能异步复位寄存器  \u_32位带使能异步复位寄存器_2  (.CLK(clk), .RESET(reset), .EN(and_2_out), .D(WD), .Q(D1));
  \_32位带使能异步复位寄存器  \u_32位带使能异步复位寄存器_3  (.CLK(clk), .RESET(reset), .EN(and_3_out), .D(WD), .Q(D2));
  \_32位带使能异步复位寄存器  \u_32位带使能异步复位寄存器_4  (.CLK(clk), .RESET(reset), .EN(and_4_out), .D(WD), .Q(D3));
  \_32位带使能异步复位寄存器  \u_32位带使能异步复位寄存器_5  (.CLK(clk), .RESET(reset), .EN(and_5_out), .D(WD), .Q(D4));
  \_32位带使能异步复位寄存器  \u_32位带使能异步复位寄存器_6  (.CLK(clk), .RESET(reset), .EN(and_6_out), .D(WD), .Q(D5));
  \_32位带使能异步复位寄存器  \u_32位带使能异步复位寄存器_7  (.CLK(clk), .RESET(reset), .EN(and_7_out), .D(WD), .Q(D6));
  \_32位带使能异步复位寄存器  \u_32位带使能异步复位寄存器_8  (.CLK(clk), .RESET(reset), .EN(and_8_out), .D(WD), .Q(D7));
  and and_9 (and_9_out, WE, WE8);
  and and_10 (and_10_out, WE, WE9);
  and and_11 (and_11_out, WE, WE10);
  and and_12 (and_12_out, WE, WE11);
  and and_13 (and_13_out, WE, WE12);
  and and_14 (and_14_out, WE, WE13);
  and and_15 (and_15_out, WE, WE14);
  and and_16 (and_16_out, WE, WE15);
  \_32位带使能异步复位寄存器  \u_32位带使能异步复位寄存器_9  (.CLK(clk), .RESET(reset), .EN(and_9_out), .D(WD), .Q(D8));
  \_32位带使能异步复位寄存器  \u_32位带使能异步复位寄存器_10  (.CLK(clk), .RESET(reset), .EN(and_10_out), .D(WD), .Q(D9));
  \_32位带使能异步复位寄存器  \u_32位带使能异步复位寄存器_11  (.CLK(clk), .RESET(reset), .EN(and_11_out), .D(WD), .Q(D10));
  \_32位带使能异步复位寄存器  \u_32位带使能异步复位寄存器_12  (.CLK(clk), .RESET(reset), .EN(and_12_out), .D(WD), .Q(D11));
  \_32位带使能异步复位寄存器  \u_32位带使能异步复位寄存器_13  (.CLK(clk), .RESET(reset), .EN(and_13_out), .D(WD), .Q(D12));
  \_32位带使能异步复位寄存器  \u_32位带使能异步复位寄存器_14  (.CLK(clk), .RESET(reset), .EN(and_14_out), .D(WD), .Q(D13));
  \_32位带使能异步复位寄存器  \u_32位带使能异步复位寄存器_15  (.CLK(clk), .RESET(reset), .EN(and_15_out), .D(WD), .Q(D14));
  \_32位带使能异步复位寄存器  \u_32位带使能异步复位寄存器_16  (.CLK(clk), .RESET(reset), .EN(and_16_out), .D(WD), .Q(D15));
  Multiplexer #(.select(5), .width(32)) multiplexer_1 (
    .in0(D0), .in1(D1), .in2(D2), .in3(D3), .in4(D4), .in5(D5), .in6(D6), .in7(D7), .in8(D8), .in9(D9),
    .in10(D10), .in11(D11), .in12(D12), .in13(D13), .in14(D14), .in15(D15), .in16(D16), .in17(D17),
    .in18(D18), .in19(D19), .in20(D20), .in21(D21), .in22(D22), .in23(D23), .in24(D24), .in25(D25),
    .in26(D26), .in27(D27), .in28(D28), .in29(D29), .in30(D30), .in31(D31), .out(RD1), .sel(A1));  // open: en
  and and_17 (and_17_out, WE, WE16);
  and and_18 (and_18_out, WE, WE17);
  and and_19 (and_19_out, WE, WE18);
  and and_20 (and_20_out, WE, WE19);
  and and_21 (and_21_out, WE, WE20);
  and and_22 (and_22_out, WE, WE21);
  and and_23 (and_23_out, WE, WE22);
  and and_24 (and_24_out, WE, WE23);
  \_32位带使能异步复位寄存器  \u_32位带使能异步复位寄存器_17  (.CLK(clk), .RESET(reset), .EN(and_17_out), .D(WD), .Q(D16));
  \_32位带使能异步复位寄存器  \u_32位带使能异步复位寄存器_18  (.CLK(clk), .RESET(reset), .EN(and_18_out), .D(WD), .Q(D17));
  \_32位带使能异步复位寄存器  \u_32位带使能异步复位寄存器_19  (.CLK(clk), .RESET(reset), .EN(and_19_out), .D(WD), .Q(D18));
  \_32位带使能异步复位寄存器  \u_32位带使能异步复位寄存器_20  (.CLK(clk), .RESET(reset), .EN(and_20_out), .D(WD), .Q(D19));
  \_32位带使能异步复位寄存器  \u_32位带使能异步复位寄存器_21  (.CLK(clk), .RESET(reset), .EN(and_21_out), .D(WD), .Q(D20));
  \_32位带使能异步复位寄存器  \u_32位带使能异步复位寄存器_22  (.CLK(clk), .RESET(reset), .EN(and_22_out), .D(WD), .Q(D21));
  \_32位带使能异步复位寄存器  \u_32位带使能异步复位寄存器_23  (.CLK(clk), .RESET(reset), .EN(and_23_out), .D(WD), .Q(D22));
  \_32位带使能异步复位寄存器  \u_32位带使能异步复位寄存器_24  (.CLK(clk), .RESET(reset), .EN(and_24_out), .D(WD), .Q(D23));
  and and_25 (and_25_out, WE, WE24);
  and and_26 (and_26_out, WE, WE25);
  and and_27 (and_27_out, WE, WE26);
  and and_28 (and_28_out, WE, WE27);
  and and_29 (and_29_out, WE, WE28);
  and and_30 (and_30_out, WE, WE29);
  and and_31 (and_31_out, WE, WE30);
  and and_32 (and_32_out, WE, WE31);
  \_32位带使能异步复位寄存器  \u_32位带使能异步复位寄存器_25  (.CLK(clk), .RESET(reset), .EN(and_25_out), .D(WD), .Q(D24));
  \_32位带使能异步复位寄存器  \u_32位带使能异步复位寄存器_26  (.CLK(clk), .RESET(reset), .EN(and_26_out), .D(WD), .Q(D25));
  \_32位带使能异步复位寄存器  \u_32位带使能异步复位寄存器_27  (.CLK(clk), .RESET(reset), .EN(and_27_out), .D(WD), .Q(D26));
  \_32位带使能异步复位寄存器  \u_32位带使能异步复位寄存器_28  (.CLK(clk), .RESET(reset), .EN(and_28_out), .D(WD), .Q(D27));
  \_32位带使能异步复位寄存器  \u_32位带使能异步复位寄存器_29  (.CLK(clk), .RESET(reset), .EN(and_29_out), .D(WD), .Q(D28));
  \_32位带使能异步复位寄存器  \u_32位带使能异步复位寄存器_30  (.CLK(clk), .RESET(reset), .EN(and_30_out), .D(WD), .Q(D29));
  \_32位带使能异步复位寄存器  \u_32位带使能异步复位寄存器_31  (.CLK(clk), .RESET(reset), .EN(and_31_out), .D(WD), .Q(D30));
  \_32位带使能异步复位寄存器  \u_32位带使能异步复位寄存器_32  (.CLK(clk), .RESET(reset), .EN(and_32_out), .D(WD), .Q(D31));
  Multiplexer #(.select(5), .width(32)) multiplexer_2 (
    .in0(D0), .in1(D1), .in2(D2), .in3(D3), .in4(D4), .in5(D5), .in6(D6), .in7(D7), .in8(D8), .in9(D9),
    .in10(D10), .in11(D11), .in12(D12), .in13(D13), .in14(D14), .in15(D15), .in16(D16), .in17(D17),
    .in18(D18), .in19(D19), .in20(D20), .in21(D21), .in22(D22), .in23(D23), .in24(D24), .in25(D25),
    .in26(D26), .in27(D27), .in28(D28), .in29(D29), .in30(D30), .in31(D31), .out(RD2), .sel(A2));  // open: en
endmodule

module \_32位带使能异步复位寄存器  (
  input  CLK,
  input  RESET,
  input  EN,
  input  [31:0] D,
  output [31:0] Q
);

  Register #(.width(32)) register_1 (.D(D), .en(EN), .Q(Q), .clk(CLK), .clr(RESET));
endmodule
