// Logisim project P0_L1_navigation_2020.circ as structural Verilog: 7 circuits, main circuit navigation
module navigation (
  input  [1:0] dir,
  input  clk,
  input  reset,
  output arrive,
  output hit
);

  wire \碰撞状态存储_1_state , \碰撞状态转移_1_next_state ;
  wire [2:0] STATE, \位置状态转移_1_next_state ;

  \位置状态转移  \u_位置状态转移_1  (.state(STATE), .dir(dir), .next_state(\位置状态转移_1_next_state ));
  \碰撞状态转移  \u_碰撞状态转移_1  (.state(STATE), .dir(dir), .next_state(\碰撞状态转移_1_next_state ));
  // Probe on STATE
  \位置状态存储  \u_位置状态存储_1  (.clk(clk), .reset(reset), .next_state(\位置状态转移_1_next_state ), .state(STATE));
  // Probe on \位置状态转移_1_next_state 
  \碰撞状态存储  \u_碰撞状态存储_1  (.clk(clk), .reset(reset), .next_state(\碰撞状态转移_1_next_state ), .state(\碰撞状态存储_1_state ));
  \位置状态输出  \u_位置状态输出_1  (.state(STATE), .signal(arrive));
  \碰撞状态输出  \u_碰撞状态输出_1  (.state(\碰撞状态存储_1_state ), .signal(hit));
endmodule

module \位置状态存储  (
  input  clk,
  input  reset,
  input  [2:0] next_state,
  output [2:0] state
);

  Register #(.width(3)) register_1 (.D(next_state), .Q(state), .clk(clk), .clr(reset));  // open: en
endmodule

module \位置状态转移  (
  input  [2:0] state,
  input  [1:0] dir,
  output [2:0] next_state
);

  wire and_1_out, and_2_out, and_3_out, and_4_out, and_5_out, and_6_out, and_7_out, and_8_out, and_9_out,
       and_10_out, not_1_out, not_2_out, not_3_out, not_4_out, not_5_out, not_6_out, not_7_out, not_8_out,
       not_9_out, not_10_out, not_11_out, not_12_out, not_13_out, not_14_out, not_15_out, not_16_out,
       not_17_out, not_18_out;

  not not_1 (not_1_out, state[0]);
  not not_2 (not_2_out, dir[1]);
  not not_3 (not_3_out, dir[1]);
  not not_4 (not_4_out, dir[0]);
  not not_5 (not_5_out, state[1]);
  not not_6 (not_6_out, dir[1]);
  not not_7 (not_7_out, dir[1]);
  not not_8 (not_8_out, state[0]);
  not not_9 (not_9_out, dir[1]);
  not not_10 (not_10_out, dir[0]);
  not not_11 (not_11_out, state[0]);
  not not_12 (not_12_out, dir[0]);
  not not_13 (not_13_out, state[2]);
  not not_14 (not_14_out, state[1]);
  not not_15 (not_15_out, state[0]);
  not not_16 (not_16_out, dir[1]);
  not not_17 (not_17_out, dir[0]);
  not not_18 (not_18_out, dir[0]);
  and and_1 (and_1_out, state[1], not_1_out, not_2_out, dir[0]);
  and and_2 (and_2_out, state[1], state[0], not_3_out, not_4_out);
  and and_3 (and_3_out, not_5_out, state[0], not_6_out);
  and and_4 (and_4_out, state[0], not_7_out, dir[0]);
  and and_5 (and_5_out, state[1], not_8_out, not_9_out, not_10_out);
  and and_6 (and_6_out, state[1], not_11_out, dir[1], dir[0]);
  and and_7 (and_7_out, state[1], state[0], dir[1], not_12_out);
  and and_8 (and_8_out, not_13_out, not_14_out, not_15_out, not_16_out, not_17_out);
  and and_9 (and_9_out, state[0], dir[0]);
  and and_10 (and_10_out, state[1], dir[1], not_18_out);
  or or_1 (next_state[2], and_1_out, and_2_out);
  or or_2 (next_state[1], and_3_out, and_4_out, and_5_out, and_6_out, and_7_out);
  or or_3 (next_state[0], and_8_out, and_9_out, and_10_out);
endmodule

module \位置状态输出  (
  input  [2:0] state,
  output signal
);

  wire not_1_out, not_2_out;

  not not_1 (not_1_out, state[0]);
  not not_2 (not_2_out, state[1]);
  and and_1 (signal, not_1_out, not_2_out, state[2]);
endmodule

module \碰撞状态存储  (
  input  clk,
  input  reset,
  input  next_state,
  output state
);

  Register #(.width(1)) register_1 (.D(next_state), .Q(state), .clk(clk), .clr(reset));  // open: en
endmodule

module \碰撞状态转移  (
  input  [2:0] state,
  input  [1:0] dir,
  output next_state
);

  wire and_1_out, and_2_out, and_3_out, and_4_out, and_5_out, and_6_out, and_7_out, not_1_out, not_2_out,
       not_3_out, not_4_out, not_5_out, not_6_out, not_7_out, not_8_out, not_9_out, not_10_out, not_11_out,
       not_12_out, not_13_out, not_14_out, not_15_out;

  not not_1 (not_1_out, state[2]);
  not not_2 (not_2_out, state[1]);
  not not_3 (not_3_out, state[0]);
  not not_4 (not_4_out, state[2]);
  not not_5 (not_5_out, state[1]);
  not not_6 (not_6_out, state[0]);
  not not_7 (not_7_out, state[2]);
  not not_8 (not_8_out, state[1]);
  not not_9 (not_9_out, state[2]);
  not not_10 (not_10_out, state[0]);
  not not_11 (not_11_out, state[0]);
  not not_12 (not_12_out, dir[1]);
  not not_13 (not_13_out, dir[0]);
  not not_14 (not_14_out, dir[1]);
  not not_15 (not_15_out, dir[0]);
  and and_1 (and_1_out, not_1_out, not_2_out, not_3_out, dir[0]);
  and and_2 (and_2_out, not_4_out, not_5_out, not_6_out, dir[1]);
  and and_3 (and_3_out, not_7_out, not_8_out, dir[1], dir[0]);
  and and_4 (and_4_out, not_9_out, not_10_out, dir[1], dir[0]);
  and and_5 (and_5_out, state[1], not_11_out, not_12_out, not_13_out);
  and and_6 (and_6_out, state[1], state[0], not_14_out, dir[0]);
  and and_7 (and_7_out, state[1], state[0], dir[1], not_15_out);
  or or_1 (next_state, and_1_out, and_2_out, and_3_out, and_4_out, and_5_out, and_6_out, and_7_out);
endmodule

module \碰撞状态输出  (
  input  state,
  output signal
);


  assign signal = state;
endmodule
