// Logisim project ftoi.circ as structural Verilog: 1 circuit, main circuit ftoi
module ftoi (
  input  [15:0] float,
  output [31:0] \int 
);

  wire and_1_out, nor_1_out, or_1_out, subtractor_1_bout;
  wire [4:0] subtractor_1_out;
  wire [31:0] multiplexer_1_out, negator_1_out, shifter_1_out;

  and and_1 (and_1_out, float[10], float[11], float[12], float[13], float[14]);
  nor nor_1 (nor_1_out, float[10], float[11], float[12], float[13], float[14]);
  Subtractor #(.width(5)) subtractor_1 (
    .a(float[14:10]), .b(5'b01111), .out(subtractor_1_out), .bout(subtractor_1_bout));  // open: bin
  or or_1 (or_1_out, and_1_out, nor_1_out, subtractor_1_bout);
  Shifter #(.width(32)) shifter_1 (.in({22'h1, float[9:0]}), .\dist (subtractor_1_out), .out(shifter_1_out));
  Multiplexer #(.width(32)) multiplexer_1 (
    .in0({{10{1'b0}}, shifter_1_out[31:10]}), .in1(negator_1_out), .out(multiplexer_1_out), .sel(float[15]));  // open: en
  Negator #(.width(32)) negator_1 (.in({{10{1'b0}}, shifter_1_out[31:10]}), .out(negator_1_out));
  Multiplexer #(.width(32)) multiplexer_2 (
    .in0(multiplexer_1_out), .in1({32{1'b0}}), .out(\int ), .sel(or_1_out));  // open: en

  // Other names for the same wires on the sheet: frac[9:0] = float[9:0]; S = float[15]
endmodule
