// Logisim project strong.circ as structural Verilog: 14 circuits, main circuit main
module main (
  input  RESET,
  output [31:0] out_2,
  output [31:0] out_3,
  output out_4,
  output [4:0] out_5,
  output [31:0] out_6,
  output out_7,
  output [31:0] out_8,
  output [31:0] out_9
);

  wire and_1_out, branch, clk, comparator_1_eq, comparator_2_eq, comparator_3_gt, comparator_4_gt,
       comparator_5_lt, comparator_6_lt, multiplexer_3_out, not_1_out, not_2_out, not_3_out;
  wire [1:0] ext_op, jump, mem_src, reg_dst, reg_src;
  wire [2:0] alu_src, cmp_ctr, mem_dst;
  wire [3:0] alu_ctr;
  wire [4:0] undriven;
  wire [31:0] adder_1_out, alu_opd1, alu_opd2, bit_extender_1_out, bit_extender_2_out, bit_extender_3_out,
       bit_extender_4_out, bit_extender_5_out, bit_extender_6_out, bit_extender_7_out, bit_extender_8_out,
       bit_extender_9_out, bit_extender_10_out, bit_extender_11_out, bit_extender_12_out,
       bit_extender_13_out, ext_1_result, mem_data, mem_output, multiplexer_6_out, multiplexer_7_out,
       multiplexer_9_out, multiplexer_10_out, multiplexer_11_out, multiplexer_12_out, next_pc, rs_base_data,
       rt_data, undriven_2;

  Clock clock_1 (.out(clk));
  // Probe on alu_src
  // Probe on branch
  // Probe on jump
  // Probe on out_3
  // Probe on out_2
  // Probe on reg_src
  // Probe on reg_dst
  // Probe on out_4
  Comparator #(.width(32)) comparator_1 (.a(alu_opd1), .b(alu_opd2), .eq(comparator_1_eq));  // open: gt, lt
  Comparator #(.width(32)) comparator_2 (.a(alu_opd1), .b(alu_opd2), .eq(comparator_2_eq));  // open: gt, lt
  not not_1 (not_1_out, comparator_2_eq);
  not not_2 (not_2_out, comparator_3_gt);
  Comparator #(.width(32)) comparator_3 (.a(alu_opd1), .b(alu_opd2), .gt(comparator_3_gt));  // open: eq, lt
  Comparator #(.width(32)) comparator_4 (.a(alu_opd1), .b(alu_opd2), .gt(comparator_4_gt));  // open: eq, lt
  Comparator #(.width(32)) comparator_5 (.a(alu_opd1), .b(alu_opd2), .lt(comparator_5_lt));  // open: gt, eq
  Comparator #(.width(32)) comparator_6 (.a(alu_opd1), .b(alu_opd2), .lt(comparator_6_lt));  // open: gt, eq
  not not_3 (not_3_out, comparator_6_lt);
  assign bit_extender_1_out = {{27{1'b0}}, out_2[10:6]};  // Bit_Extender bit_extender_1
  EXT ext_1 (.OPRD(out_2[15:0]), .OP(ext_op), .RESULT(ext_1_result));
  Multiplexer #(.select(2), .width(32)) multiplexer_1 (
    .in0(rt_data), .in1(ext_1_result), .in2({32{1'b0}}), .out(alu_opd2), .sel(alu_src[2:1]));  // open: in3, en
  Multiplexer #(.width(32)) multiplexer_2 (
    .in0(rs_base_data), .in1(bit_extender_1_out), .out(alu_opd1), .sel(alu_src[0]));  // open: en
  // Probe on out_2[25:21]
  // Probe on out_2[20:16]
  // Probe on out_2[15:11]
  // Probe on mem_src
  // Probe on mem_dst
  // Probe on out_7
  Multiplexer #(.select(3)) multiplexer_3 (
    .in0(comparator_1_eq), .in1(not_1_out), .in2(not_2_out), .in3(comparator_4_gt), .in4(comparator_5_lt),
    .in5(not_3_out), .in6(1'b0), .in7(1'b0), .out(multiplexer_3_out), .sel(cmp_ctr));  // open: en
  ALU alu_1 (.OPRD1(alu_opd1), .OPRD2(alu_opd2), .OP(alu_ctr), .RESULT(out_8));
  // Probe on out_2[15:0]
  // Probe on out_2[15:0]
  // Probe on out_2[15:0]
  and and_1 (and_1_out, branch, multiplexer_3_out);
  // Probe on ext_op
  // Probe on alu_ctr
  // Probe on cmp_ctr
  NPC npc_1 (
    .PC(out_3), .OFFSET(out_2[15:0]), .INDEX(out_2[25:0]), .RA(rs_base_data), .BRANCH(and_1_out),
    .JUMP(jump), .NPC(next_pc));
  IFU ifu_1 (.NEXT_PC(next_pc), .CLK(clk), .RESET(RESET), .PC(out_3), .INSTR(out_2));
  // Probe on rt_data
  // Probe on rt_data
  // Probe on rt_data
  Multiplexer #(.select(2), .width(5)) multiplexer_4 (
    .in0(out_2[20:16]), .in1(out_2[15:11]), .in2({5{1'b1}}), .in3(undriven), .out(out_5), .sel(reg_dst));  // open: en
  Multiplexer #(.select(2), .width(32)) multiplexer_5 (
    .in0(out_8), .in1(mem_data), .in2(adder_1_out), .in3(undriven_2), .out(out_6), .sel(reg_src));  // open: en
  Adder #(.width(32)) adder_1 (.a(out_3), .b(32'h4), .out(adder_1_out));  // open: cin, cout
  // Probe on rs_base_data
  // Probe on rs_base_data
  // Probe on rs_base_data
  GRF grf_1 (
    .RA1(out_2[25:21]), .RA2(out_2[20:16]), .WE(out_4), .WA(out_5), .WD(out_6), .clk(clk), .reset(RESET),
    .RD1(rs_base_data), .RD2(rt_data));
  // Probe on out_5
  // Probe on out_6
  // Probe on out_6
  // Probe on out_6
  // Probe on out_9
  // Probe on out_9
  // Probe on out_9
  // Probe on mem_output
  // Probe on mem_output
  // Probe on mem_output
  Controller controller_1 (
    .OP(out_2[31:26]), .FUNC(out_2[5:0]), .RT(out_2[20:16]), .ALUSrc(alu_src), .RegSrc(reg_src),
    .RegDst(reg_dst), .RegWrite(out_4), .MemSrc(mem_src), .MemDst(mem_dst), .MemWrite(out_7),
    .BRANCH(branch), .JUMP(jump), .ExtOp(ext_op), .ALUCtr(alu_ctr), .CmpCtr(cmp_ctr));
  Multiplexer #(.select(2), .width(32)) multiplexer_6 (
    .in0({mem_data[31:8], rt_data[7:0]}), .in1({mem_data[31:16], rt_data[7:0], mem_data[7:0]}),
    .in2({mem_data[31:24], rt_data[7:0], mem_data[15:0]}), .in3({rt_data[7:0], mem_data[23:0]}),
    .out(multiplexer_6_out), .sel(out_8[1:0]));  // open: en
  Multiplexer #(.width(32)) multiplexer_7 (
    .in0({mem_data[31:16], rt_data[15:0]}), .in1({rt_data[15:0], mem_data[15:0]}), .out(multiplexer_7_out),
    .sel(out_8[1]));  // open: en
  Multiplexer #(.select(2), .width(32)) multiplexer_8 (
    .in0(multiplexer_6_out), .in1(multiplexer_7_out), .in2(rt_data), .in3(rt_data), .out(out_9), .sel(mem_src));  // open: en
  // Probe on alu_opd1
  // Probe on alu_opd1
  // Probe on alu_opd1
  // Probe on alu_opd2
  // Probe on alu_opd2
  // Probe on alu_opd2
  DM dm_1 (.WE(out_7), .ADDR(out_8), .WD(out_9), .CLK(clk), .RESET(RESET), .RD(mem_data));
  // Probe on out_8
  // Probe on out_8
  // Probe on out_8
  // Probe on next_pc
  assign bit_extender_2_out = {{24{mem_data[7]}}, mem_data[7:0]};  // Bit_Extender bit_extender_2
  assign bit_extender_3_out = {{24{mem_data[15]}}, mem_data[15:8]};  // Bit_Extender bit_extender_3
  assign bit_extender_4_out = {{24{mem_data[23]}}, mem_data[23:16]};  // Bit_Extender bit_extender_4
  assign bit_extender_5_out = {{24{mem_data[31]}}, mem_data[31:24]};  // Bit_Extender bit_extender_5
  assign bit_extender_6_out = {{16{mem_data[15]}}, mem_data[15:0]};  // Bit_Extender bit_extender_6
  assign bit_extender_7_out = {{16{mem_data[31]}}, mem_data[31:16]};  // Bit_Extender bit_extender_7
  assign bit_extender_8_out = {{24{1'b0}}, mem_data[7:0]};  // Bit_Extender bit_extender_8
  assign bit_extender_9_out = {{24{1'b0}}, mem_data[15:8]};  // Bit_Extender bit_extender_9
  assign bit_extender_10_out = {{24{1'b0}}, mem_data[23:16]};  // Bit_Extender bit_extender_10
  assign bit_extender_11_out = {{24{1'b0}}, mem_data[31:24]};  // Bit_Extender bit_extender_11
  assign bit_extender_12_out = {{16{1'b0}}, mem_data[15:0]};  // Bit_Extender bit_extender_12
  assign bit_extender_13_out = {{16{1'b0}}, mem_data[31:16]};  // Bit_Extender bit_extender_13
  Multiplexer #(.select(2), .width(32)) multiplexer_9 (
    .in0(bit_extender_2_out), .in1(bit_extender_3_out), .in2(bit_extender_4_out), .in3(bit_extender_5_out),
    .out(multiplexer_9_out), .sel(out_8[1:0]));  // open: en
  Multiplexer #(.width(32)) multiplexer_10 (
    .in0(bit_extender_6_out), .in1(bit_extender_7_out), .out(multiplexer_10_out), .sel(out_8[1]));  // open: en
  Multiplexer #(.select(2), .width(32)) multiplexer_11 (
    .in0(bit_extender_8_out), .in1(bit_extender_9_out), .in2(bit_extender_10_out), .in3(bit_extender_11_out),
    .out(multiplexer_11_out), .sel(out_8[1:0]));  // open: en
  Multiplexer #(.width(32)) multiplexer_12 (
    .in0(bit_extender_12_out), .in1(bit_extender_13_out), .out(multiplexer_12_out), .sel(out_8[1]));  // open: en
  Multiplexer #(.select(3), .width(32)) multiplexer_13 (
    .in0(multiplexer_9_out), .in1(multiplexer_10_out), .in2(mem_data), .in3(multiplexer_11_out),
    .in4(multiplexer_12_out), .in5(mem_data), .in6(mem_data), .in7(mem_data), .out(mem_output), .sel(mem_dst));  // open: en

  // Other names for the same wires on the sheet: mem_data16_23[7:0] = mem_data[23:16];
  //   mem_data16_31[15:0] = mem_data[31:16]; mem_data24_31[7:0] = mem_data[31:24]; mem_data0_7[7:0] = mem_data[7:0];
  //   mem_data0_15[15:0] = mem_data[15:0]; mem_data8_15[7:0] = mem_data[15:8]; rt_data_byte[7:0] = rt_data[7:0];
  //   rt_data_half[15:0] = rt_data[15:0]; alu_result[31:0] = out_8; func[5:0] = out_2[5:0];
  //   imm_off[15:0] = out_2[15:0]; index[25:0] = out_2[25:0]; instr[31:0] = out_2; s[4:0] = out_2[10:6];
  //   rd[4:0] = out_2[15:11]; rt[4:0] = out_2[20:16]; rs_base[4:0] = out_2[25:21]; op[5:0] = out_2[31:26];
  //   mem_input[31:0] = out_9; mem_write = out_7; pc[31:0] = out_3; reg_input[31:0] = out_6;
  //   reg_input_to[4:0] = out_5; reg_write = out_4
endmodule

module IFU (
  input  CLK,
  input  RESET,
  input  [31:0] NEXT_PC,
  output [31:0] PC,
  output [31:0] INSTR
);

  // Probe on PC
  IM IM (.ADDR(PC), .DATA(INSTR));
  PC u_PC (.CLK(CLK), .RESET(RESET), .NEXT(NEXT_PC), .ADDR(PC));
  // Probe on INSTR

  // Other names for the same wires on the sheet: addr[31:0] = NEXT_PC
endmodule

module PC (
  input  CLK,
  input  RESET,
  input  [31:0] NEXT,
  output [31:0] ADDR
);

  \_32位带范围异步复位寄存器  \u_32位带范围异步复位寄存器_1  (.CLK(CLK), .RESET(RESET), .MIN(32'h3000), .MAX(32'h6fff), .D(NEXT), .Q(ADDR));
  // Probe on ADDR
endmodule

module NPC (
  input  [31:0] PC,
  input  [15:0] OFFSET,
  input  [25:0] INDEX,
  input  [31:0] RA,
  input  BRANCH,
  input  [1:0] JUMP,
  output [31:0] NPC
);

  wire [31:0] adder_1_out, adder_2_out, bit_extender_1_out, multiplexer_1_out, multiplexer_2_out;

  Adder #(.width(32)) adder_1 (.a(PC), .b(32'h4), .out(adder_1_out));  // open: cin, cout
  Adder #(.width(32)) adder_2 (.a(adder_1_out), .b(bit_extender_1_out), .out(adder_2_out));  // open: cin, cout
  assign bit_extender_1_out = {{14{OFFSET[15]}}, {OFFSET, 2'b00}};  // Bit_Extender bit_extender_1
  Multiplexer #(.width(32)) multiplexer_1 (
    .in0(adder_1_out), .in1(adder_2_out), .out(multiplexer_1_out), .sel(BRANCH));  // open: en
  Multiplexer #(.width(32)) multiplexer_2 (
    .in0({PC[31:28], INDEX, 2'b00}), .in1(RA), .out(multiplexer_2_out), .sel(JUMP[1]));  // open: en
  Multiplexer #(.width(32)) multiplexer_3 (
    .in0(multiplexer_1_out), .in1(multiplexer_2_out), .out(NPC), .sel(JUMP[0]));  // open: en

  // Other names for the same wires on the sheet: addr[31:2] = {PC[31:28], INDEX}
endmodule

module \_32位带范围异步复位寄存器  (
  input  CLK,
  input  RESET,
  input  [31:0] MIN,
  input  [31:0] MAX,
  input  [31:0] D,
  output [31:0] Q
);

  wire comparator_1_gt;
  wire [31:0] multiplexer_1_out, register_1_q, xor_1_out, xor_2_out;

  assign xor_1_out = MIN ^ D;  // XOR_Gate xor_1, 32 bits wide
  assign xor_2_out = MIN ^ MIN;  // XOR_Gate xor_2, 32 bits wide
  Comparator #(.width(32), .mode("unsigned")) comparator_1 (.a(D), .b(MAX), .gt(comparator_1_gt));  // open: eq, lt
  Multiplexer #(.width(32)) multiplexer_1 (
    .in0(xor_1_out), .in1(xor_2_out), .out(multiplexer_1_out), .sel(comparator_1_gt));  // open: en
  Register #(.width(32)) register_1 (.D(multiplexer_1_out), .Q(register_1_q), .clk(CLK), .clr(RESET));  // open: en
  assign Q = MIN ^ register_1_q;  // XOR_Gate xor_3, 32 bits wide
endmodule

module IM (
  input  [31:0] ADDR,
  output [31:0] DATA
);

  wire [31:0] shifter_1_out, subtractor_1_out;

  // Probe on ADDR
  Subtractor #(.width(32)) subtractor_1 (.a(ADDR), .b(32'h3000), .out(subtractor_1_out));  // open: bin, bout
  Shifter #(.width(32), .shift("lr")) shifter_1 (.in(subtractor_1_out), .\dist (5'b00010), .out(shifter_1_out));
  ROM #(.addrWidth(12), .dataWidth(32)) rom_1 (.addr(shifter_1_out[11:0]), .data(DATA));  // open: sel
  // Probe on DATA

  // Notes on the sheet:
  //   contents of rom_1 (hex, n*v repeats v):
  //   24110001 00000000 02318820 02318820 02318820 02318820 02318820 02318820 02318820 02318820 02318820
  //   02318820 02318820 02318820 02318820 02318820 02318820 02318820 02318820 02318820 02318820 02318820
  //   02318820 02318820 02318820 02318820 02318820 02318820 02318820 02318820 02318820 02318820 02318820
  //   02318820 02318820 02318820 02318820 02318820 02318820 02318820 02318820 02318820 02318820 02318820
  //   02318820 02318820 02318820 02318820 02318820 02318820 02318820 02318820 02318820 02318820 02318820
  //   02318820 02318820 02318820 02318820 02318820 02318820 02318820 02318820 02318820 02318820 02318820
  //   02318820 02318820 02318820 02318820 02318820 02318820 02318820 02318820 02318820 02318820 02318820
  //   02318820 02318820 02318820 02318820 02318820 02318820 02318820 02318820 02318820 02318820 02318820
  //   02318820 02318820 02318820 02318820 02318820 02318820 02318820 02318820 02318820 02318820 02318820
  //   02318820 02318820 02318820 02318820 02318820 02318820 02318820 02318820 02318820 02318820 02318820
  //   02318820 02318820 02318820 02318820 02318820 02318820 02318820 02318820 02318820 02318820 02318820
  //   02318820 02318820 02318820 02318820 02318820 02318820 02318820 02318820 02318820 02318820 02318820
  //   02318820 02318820 02318820 02318820 02318820 02318820 02318820 02318820 02318820 02318820 02318820
  //   02318820 02318820 02318820 02318820 02318820 02318820 02318820 02318820 02318820 02318820 02318820
  //   02318820 02318820 02318820 02318820 02318820 02318820 02318820 02318820 02318820 02318820 02318820
  //   02318820 02318820 02318820 02318820 02318820 02318820 02318820 02318820 02318820 02318820 02318820
  //   02318820 02318820 02318820 02318820 02318820 02318820 02318820 02318820 02318820 02318820 02318820
  //   02318820 02318820 02318820 02318820 02318820 02318820 02318820
endmodule

module GRF (
  input  clk,
  input  reset,
  input  [4:0] RA1,
  input  [4:0] RA2,
  input  WE,
  input  [4:0] WA,
  input  [31:0] WD,
  output [31:0] RD1,
  output [31:0] RD2
);

  wire and_1_out, and_2_out, and_3_out, and_4_out, and_5_out, and_6_out, and_7_out, and_8_out, and_9_out,
       and_10_out, and_11_out, and_12_out, and_13_out, and_14_out, and_15_out, and_16_out, and_17_out,
       and_18_out, and_19_out, and_20_out, and_21_out, and_22_out, and_23_out, and_24_out, and_25_out,
       and_26_out, and_27_out, and_28_out, and_29_out, and_30_out, and_31_out, and_32_out, WE0, WE1, WE2,
       WE3, WE4, WE5, WE6, WE7, WE8, WE9, WE10, WE11, WE12, WE13, WE14, WE15, WE16, WE17, WE18, WE19, WE20,
       WE21, WE22, WE23, WE24, WE25, WE26, WE27, WE28, WE29, WE30, WE31;
  wire [31:0] D0, D1, D2, D3, D4, D5, D6, D7, D8, D9, D10, D11, D12, D13, D14, D15, D16, D17, D18, D19, D20,
       D21, D22, D23, D24, D25, D26, D27, D28, D29, D30, D31;

  Decoder #(.select(5)) decoder_1 (
    .out0(WE0), .out1(WE1), .out2(WE2), .out3(WE3), .out4(WE4), .out5(WE5), .out6(WE6), .out7(WE7),
    .out8(WE8), .out9(WE9), .out10(WE10), .out11(WE11), .out12(WE12), .out13(WE13), .out14(WE14),
    .out15(WE15), .out16(WE16), .out17(WE17), .out18(WE18), .out19(WE19), .out20(WE20), .out21(WE21),
    .out22(WE22), .out23(WE23), .out24(WE24), .out25(WE25), .out26(WE26), .out27(WE27), .out28(WE28),
    .out29(WE29), .out30(WE30), .out31(WE31), .sel(WA));  // open: en
  and and_1 (and_1_out, WE, WE0);
  and and_2 (and_2_out, WE, WE1);
  and and_3 (and_3_out, WE, WE2);
  and and_4 (and_4_out, WE, WE3);
  and and_5 (and_5_out, WE, WE4);
  and and_6 (and_6_out, WE, WE5);
  and and_7 (and_7_out, WE, WE6);
  and and_8 (and_8_out, WE, WE7);
  \_32位带使能异步复位寄存器  \u_32位带使能异步复位寄存器_1  (.CLK(clk), .RESET(reset), .EN(and_1_out), .D({32{1'b0}}), .Q(D0));
  \_32位带使能异步复位寄存器  \u_32位带使能异步复位寄存器_2  (.CLK(clk), .RESET(reset), .EN(and_2_out), .D(WD), .Q(D1));
  \_32位带使能异步复位寄存器  \u_32位带使能异步复位寄存器_3  (.CLK(clk), .RESET(reset), .EN(and_3_out), .D(WD), .Q(D2));
  \_32位带使能异步复位寄存器  \u_32位带使能异步复位寄存器_4  (.CLK(clk), .RESET(reset), .EN(and_4_out), .D(WD), .Q(D3));
  \_32位带使能异步复位寄存器  \u_32位带使能异步复位寄存器_5  (.CLK(clk), .RESET(reset), .EN(and_5_out), .D(WD), .Q(D4));
  \_32位带使能异步复位寄存器  \u_32位带使能异步复位寄存器_6  (.CLK(clk), .RESET(reset), .EN(and_6_out), .D(WD), .Q(D5));
  \_32位带使能异步复位寄存器  \u_32位带使能异步复位寄存器_7  (.CLK(clk), .RESET(reset), .EN(and_7_out), .D(WD), .Q(D6));
  \_32位带使能异步复位寄存器  \u_32位带使能异步复位寄存器_8  (.CLK(clk), .RESET(reset), .EN(and_8_out), .D(WD), .Q(D7));
  and and_9 (and_9_out, WE, WE8);
  and and_10 (and_10_out, WE, WE9);
  and and_11 (and_11_out, WE, WE10);
  and and_12 (and_12_out, WE, WE11);
  and and_13 (and_13_out, WE, WE12);
  and and_14 (and_14_out, WE, WE13);
  and and_15 (and_15_out, WE, WE14);
  and and_16 (and_16_out, WE, WE15);
  \_32位带使能异步复位寄存器  \u_32位带使能异步复位寄存器_9  (.CLK(clk), .RESET(reset), .EN(and_9_out), .D(WD), .Q(D8));
  \_32位带使能异步复位寄存器  \u_32位带使能异步复位寄存器_10  (.CLK(clk), .RESET(reset), .EN(and_10_out), .D(WD), .Q(D9));
  \_32位带使能异步复位寄存器  \u_32位带使能异步复位寄存器_11  (.CLK(clk), .RESET(reset), .EN(and_11_out), .D(WD), .Q(D10));
  \_32位带使能异步复位寄存器  \u_32位带使能异步复位寄存器_12  (.CLK(clk), .RESET(reset), .EN(and_12_out), .D(WD), .Q(D11));
  \_32位带使能异步复位寄存器  \u_32位带使能异步复位寄存器_13  (.CLK(clk), .RESET(reset), .EN(and_13_out), .D(WD), .Q(D12));
  \_32位带使能异步复位寄存器  \u_32位带使能异步复位寄存器_14  (.CLK(clk), .RESET(reset), .EN(and_14_out), .D(WD), .Q(D13));
  \_32位带使能异步复位寄存器  \u_32位带使能异步复位寄存器_15  (.CLK(clk), .RESET(reset), .EN(and_15_out), .D(WD), .Q(D14));
  \_32位带使能异步复位寄存器  \u_32位带使能异步复位寄存器_16  (.CLK(clk), .RESET(reset), .EN(and_16_out), .D(WD), .Q(D15));
  Multiplexer #(.select(5), .width(32)) multiplexer_1 (
    .in0(D0), .in1(D1), .in2(D2), .in3(D3), .in4(D4), .in5(D5), .in6(D6), .in7(D7), .in8(D8), .in9(D9),
    .in10(D10), .in11(D11), .in12(D12), .in13(D13), .in14(D14), .in15(D15), .in16(D16), .in17(D17),
    .in18(D18), .in19(D19), .in20(D20), .in21(D21), .in22(D22), .in23(D23), .in24(D24), .in25(D25),
    .in26(D26), .in27(D27), .in28(D28), .in29(D29), .in30(D30), .in31(D31), .out(RD1), .sel(RA1));  // open: en
  and and_17 (and_17_out, WE, WE16);
  and and_18 (and_18_out, WE, WE17);
  and and_19 (and_19_out, WE, WE18);
  and and_20 (and_20_out, WE, WE19);
  and and_21 (and_21_out, WE, WE20);
  and and_22 (and_22_out, WE, WE21);
  and and_23 (and_23_out, WE, WE22);
  and and_24 (and_24_out, WE, WE23);
  \_32位带使能异步复位寄存器  \u_32位带使能异步复位寄存器_17  (.CLK(clk), .RESET(reset), .EN(and_17_out), .D(WD), .Q(D16));
  \_32位带使能异步复位寄存器  \u_32位带使能异步复位寄存器_18  (.CLK(clk), .RESET(reset), .EN(and_18_out), .D(WD), .Q(D17));
  \_32位带使能异步复位寄存器  \u_32位带使能异步复位寄存器_19  (.CLK(clk), .RESET(reset), .EN(and_19_out), .D(WD), .Q(D18));
  \_32位带使能异步复位寄存器  \u_32位带使能异步复位寄存器_20  (.CLK(clk), .RESET(reset), .EN(and_20_out), .D(WD), .Q(D19));
  \_32位带使能异步复位寄存器  \u_32位带使能异步复位寄存器_21  (.CLK(clk), .RESET(reset), .EN(and_21_out), .D(WD), .Q(D20));
  \_32位带使能异步复位寄存器  \u_32位带使能异步复位寄存器_22  (.CLK(clk), .RESET(reset), .EN(and_22_out), .D(WD), .Q(D21));
  \_32位带使能异步复位寄存器  \u_32位带使能异步复位寄存器_23  (.CLK(clk), .RESET(reset), .EN(and_23_out), .D(WD), .Q(D22));
  \_32位带使能异步复位寄存器  \u_32位带使能异步复位寄存器_24  (.CLK(clk), .RESET(reset), .EN(and_24_out), .D(WD), .Q(D23));
  and and_25 (and_25_out, WE, WE24);
  and and_26 (and_26_out, WE, WE25);
  and and_27 (and_27_out, WE, WE26);
  and and_28 (and_28_out, WE, WE27);
  and and_29 (and_29_out, WE, WE28);
  and and_30 (and_30_out, WE, WE29);
  and and_31 (and_31_out, WE, WE30);
  and and_32 (and_32_out, WE, WE31);
  \_32位带使能异步复位寄存器  \u_32位带使能异步复位寄存器_25  (.CLK(clk), .RESET(reset), .EN(and_25_out), .D(WD), .Q(D24));
  \_32位带使能异步复位寄存器  \u_32位带使能异步复位寄存器_26  (.CLK(clk), .RESET(reset), .EN(and_26_out), .D(WD), .Q(D25));
  \_32位带使能异步复位寄存器  \u_32位带使能异步复位寄存器_27  (.CLK(clk), .RESET(reset), .EN(and_27_out), .D(WD), .Q(D26));
  \_32位带使能异步复位寄存器  \u_32位带使能异步复位寄存器_28  (.CLK(clk), .RESET(reset), .EN(and_28_out), .D(WD), .Q(D27));
  \_32位带使能异步复位寄存器  \u_32位带使能异步复位寄存器_29  (.CLK(clk), .RESET(reset), .EN(and_29_out), .D(WD), .Q(D28));
  \_32位带使能异步复位寄存器  \u_32位带使能异步复位寄存器_30  (.CLK(clk), .RESET(reset), .EN(and_30_out), .D(WD), .Q(D29));
  \_32位带使能异步复位寄存器  \u_32位带使能异步复位寄存器_31  (.CLK(clk), .RESET(reset), .EN(and_31_out), .D(WD), .Q(D30));
  \_32位带使能异步复位寄存器  \u_32位带使能异步复位寄存器_32  (.CLK(clk), .RESET(reset), .EN(and_32_out), .D(WD), .Q(D31));
  Multiplexer #(.select(5), .width(32)) multiplexer_2 (
    .in0(D0), .in1(D1), .in2(D2), .in3(D3), .in4(D4), .in5(D5), .in6(D6), .in7(D7), .in8(D8), .in9(D9),
    .in10(D10), .in11(D11), .in12(D12), .in13(D13), .in14(D14), .in15(D15), .in16(D16), .in17(D17),
    .in18(D18), .in19(D19), .in20(D20), .in21(D21), .in22(D22), .in23(D23), .in24(D24), .in25(D25),
    .in26(D26), .in27(D27), .in28(D28), .in29(D29), .in30(D30), .in31(D31), .out(RD2), .sel(RA2));  // open: en

  // Other names for the same wires on the sheet: A1[4:0] = RA1; A2[4:0] = RA2; A3[4:0] = WA
endmodule

module \_32位带使能异步复位寄存器  (
  input  CLK,
  input  RESET,
  input  EN,
  input  [31:0] D,
  output [31:0] Q
);

  Register #(.width(32)) register_1 (.D(D), .en(EN), .Q(Q), .clk(CLK), .clr(RESET));
endmodule

module ALU (
  input  [31:0] OPRD1,
  input  [31:0] OPRD2,
  input  [3:0] OP,
  output [31:0] RESULT
);

  wire comparator_1_lt, comparator_2_lt;
  wire [31:0] adder_1_out, and_1_out, bit_extender_1_out, bit_extender_2_out, nor_1_out, or_1_out,
       shifter_1_out, shifter_2_out, shifter_3_out, subtractor_1_out, xor_1_out;

  Adder #(.width(32)) adder_1 (.a(OPRD1), .b(OPRD2), .out(adder_1_out));  // open: cin, cout
  Subtractor #(.width(32)) subtractor_1 (.a(OPRD1), .b(OPRD2), .out(subtractor_1_out));  // open: bin, bout
  assign and_1_out = OPRD1 & OPRD2;  // AND_Gate and_1, 32 bits wide
  assign or_1_out = OPRD1 | OPRD2;  // OR_Gate or_1, 32 bits wide
  assign xor_1_out = OPRD1 ^ OPRD2;  // XOR_Gate xor_1, 32 bits wide
  assign nor_1_out = ~(OPRD1 | OPRD2);  // NOR_Gate nor_1, 32 bits wide
  Shifter #(.width(32)) shifter_1 (.in(OPRD2), .\dist (OPRD1[4:0]), .out(shifter_1_out));
  Shifter #(.width(32), .shift("lr")) shifter_2 (.in(OPRD2), .\dist (OPRD1[4:0]), .out(shifter_2_out));
  Shifter #(.width(32), .shift("ar")) shifter_3 (.in(OPRD2), .\dist (OPRD1[4:0]), .out(shifter_3_out));
  Comparator #(.width(32)) comparator_1 (.a(OPRD1), .b(OPRD2), .lt(comparator_1_lt));  // open: gt, eq
  Comparator #(.width(32), .mode("unsigned")) comparator_2 (
    .a(OPRD1), .b(OPRD2), .lt(comparator_2_lt));  // open: gt, eq
  assign bit_extender_1_out = {{31{1'b0}}, comparator_1_lt};  // Bit_Extender bit_extender_1
  assign bit_extender_2_out = {{31{1'b0}}, comparator_2_lt};  // Bit_Extender bit_extender_2
  Multiplexer #(.select(4), .width(32)) multiplexer_1 (
    .in0(adder_1_out), .in1(subtractor_1_out), .in2(and_1_out), .in3(or_1_out), .in4(xor_1_out),
    .in5(nor_1_out), .in6(shifter_1_out), .in7(shifter_2_out), .in8(shifter_3_out), .in9(bit_extender_1_out),
    .in10(bit_extender_2_out), .in15({32{1'b0}}), .out(RESULT), .sel(OP));  // open: in11, in12, in13, in14, en

  // Other names for the same wires on the sheet: oprd1_5[4:0] = OPRD1[4:0]
endmodule

module DM (
  input  CLK,
  input  RESET,
  input  WE,
  input  [31:0] ADDR,
  input  [31:0] WD,
  output [31:0] RD
);

  wire [31:0] shifter_1_out;

  // Probe on ADDR
  // Probe on WD
  Shifter #(.width(32), .shift("lr")) shifter_1 (.in(ADDR), .\dist (5'b00010), .out(shifter_1_out));
  RAM #(.addrWidth(12), .dataWidth(32), .bus("separate")) ram_1 (
    .addr(shifter_1_out[11:0]), .din(WD), .data(RD), .str(WE), .clk(CLK), .clr(RESET));  // open: sel, ld
  // Probe on RD
endmodule

module EXT (
  input  [15:0] OPRD,
  input  [1:0] OP,
  output [31:0] RESULT
);

  wire [31:0] bit_extender_1_out, bit_extender_2_out, bit_extender_3_out, shifter_1_out;

  // Probe on OPRD
  assign bit_extender_1_out = {{16{1'b0}}, OPRD};  // Bit_Extender bit_extender_1
  assign bit_extender_2_out = {{16{OPRD[15]}}, OPRD};  // Bit_Extender bit_extender_2
  assign bit_extender_3_out = {{16{OPRD[15]}}, OPRD};  // Bit_Extender bit_extender_3
  Shifter #(.width(32)) shifter_1 (.in(bit_extender_3_out), .\dist (5'b00010), .out(shifter_1_out));
  Multiplexer #(.select(2), .width(32)) multiplexer_1 (
    .in0(bit_extender_1_out), .in1(bit_extender_2_out), .in2({OPRD, {16{1'b0}}}), .in3(shifter_1_out),
    .out(RESULT), .sel(OP));  // open: en
  // Probe on RESULT
endmodule

module Controller (
  input  [5:0] OP,
  input  [5:0] FUNC,
  input  [4:0] RT,
  output [2:0] ALUSrc,
  output [1:0] RegSrc,
  output [1:0] RegDst,
  output RegWrite,
  output [1:0] MemSrc,
  output [2:0] MemDst,
  output MemWrite,
  output BRANCH,
  output [1:0] JUMP,
  output [1:0] ExtOp,
  output [3:0] ALUCtr,
  output [2:0] CmpCtr
);

  wire \指令信号生成器_1_add , \指令信号生成器_1_addi , \指令信号生成器_1_addiu , \指令信号生成器_1_addu , \指令信号生成器_1_and ,
       \指令信号生成器_1_andi , \指令信号生成器_1_beq , \指令信号生成器_1_bgez , \指令信号生成器_1_bgezal , \指令信号生成器_1_bgtz ,
       \指令信号生成器_1_blez , \指令信号生成器_1_bltz , \指令信号生成器_1_bltzal , \指令信号生成器_1_bne , \指令信号生成器_1_j ,
       \指令信号生成器_1_jal , \指令信号生成器_1_jalr , \指令信号生成器_1_jr , \指令信号生成器_1_lb , \指令信号生成器_1_lbu , \指令信号生成器_1_lh ,
       \指令信号生成器_1_lhu , \指令信号生成器_1_lui , \指令信号生成器_1_lw , \指令信号生成器_1_nor , \指令信号生成器_1_or , \指令信号生成器_1_ori ,
       \指令信号生成器_1_sb , \指令信号生成器_1_sh , \指令信号生成器_1_sll , \指令信号生成器_1_sllv , \指令信号生成器_1_slt , \指令信号生成器_1_slti ,
       \指令信号生成器_1_sltiu , \指令信号生成器_1_sltu , \指令信号生成器_1_sra , \指令信号生成器_1_srav , \指令信号生成器_1_srl ,
       \指令信号生成器_1_srlv , \指令信号生成器_1_sub , \指令信号生成器_1_subu , \指令信号生成器_1_sw , \指令信号生成器_1_xor , \指令信号生成器_1_xori ;

  \指令信号生成器  \u_指令信号生成器_1  (
    .OP(OP), .FUNC(FUNC), .RT(RT), .ADD(\指令信号生成器_1_add ), .ADDU(\指令信号生成器_1_addu ), .SUB(\指令信号生成器_1_sub ),
    .SUBU(\指令信号生成器_1_subu ), .ADDI(\指令信号生成器_1_addi ), .ADDIU(\指令信号生成器_1_addiu ), .SLTI(\指令信号生成器_1_slti ),
    .SLTIU(\指令信号生成器_1_sltiu ), .SLT(\指令信号生成器_1_slt ), .SLTU(\指令信号生成器_1_sltu ), .BEQ(\指令信号生成器_1_beq ),
    .BNE(\指令信号生成器_1_bne ), .BLEZ(\指令信号生成器_1_blez ), .BGTZ(\指令信号生成器_1_bgtz ), .BLTZ(\指令信号生成器_1_bltz ),
    .BGEZ(\指令信号生成器_1_bgez ), .BLTZAL(\指令信号生成器_1_bltzal ), .BGEZAL(\指令信号生成器_1_bgezal ), .J(\指令信号生成器_1_j ),
    .JAL(\指令信号生成器_1_jal ), .JR(\指令信号生成器_1_jr ), .JALR(\指令信号生成器_1_jalr ), .LB(\指令信号生成器_1_lb ),
    .LH(\指令信号生成器_1_lh ), .LW(\指令信号生成器_1_lw ), .LBU(\指令信号生成器_1_lbu ), .LHU(\指令信号生成器_1_lhu ),
    .SB(\指令信号生成器_1_sb ), .SH(\指令信号生成器_1_sh ), .SW(\指令信号生成器_1_sw ), .AND(\指令信号生成器_1_and ),
    .OR(\指令信号生成器_1_or ), .XOR(\指令信号生成器_1_xor ), .NOR(\指令信号生成器_1_nor ), .ANDI(\指令信号生成器_1_andi ),
    .ORI(\指令信号生成器_1_ori ), .XORI(\指令信号生成器_1_xori ), .LUI(\指令信号生成器_1_lui ), .SLL(\指令信号生成器_1_sll ),
    .SRL(\指令信号生成器_1_srl ), .SRA(\指令信号生成器_1_sra ), .SLLV(\指令信号生成器_1_sllv ), .SRLV(\指令信号生成器_1_srlv ),
    .SRAV(\指令信号生成器_1_srav ));
  \控制信号生成器  \u_控制信号生成器_1  (
    .ADD(\指令信号生成器_1_add ), .ADDU(\指令信号生成器_1_addu ), .SUB(\指令信号生成器_1_sub ), .SUBU(\指令信号生成器_1_subu ),
    .ADDI(\指令信号生成器_1_addi ), .ADDIU(\指令信号生成器_1_addiu ), .SLTI(\指令信号生成器_1_slti ), .SLTIU(\指令信号生成器_1_sltiu ),
    .SLT(\指令信号生成器_1_slt ), .SLTU(\指令信号生成器_1_sltu ), .BEQ(\指令信号生成器_1_beq ), .BNE(\指令信号生成器_1_bne ),
    .BLEZ(\指令信号生成器_1_blez ), .BGTZ(\指令信号生成器_1_bgtz ), .BLTZ(\指令信号生成器_1_bltz ), .BGEZ(\指令信号生成器_1_bgez ),
    .BLTZAL(\指令信号生成器_1_bltzal ), .BGEZAL(\指令信号生成器_1_bgezal ), .J(\指令信号生成器_1_j ), .JAL(\指令信号生成器_1_jal ),
    .JR(\指令信号生成器_1_jr ), .JRAL(\指令信号生成器_1_jalr ), .LB(\指令信号生成器_1_lb ), .LH(\指令信号生成器_1_lh ),
    .LW(\指令信号生成器_1_lw ), .LBU(\指令信号生成器_1_lbu ), .LHU(\指令信号生成器_1_lhu ), .SB(\指令信号生成器_1_sb ),
    .SH(\指令信号生成器_1_sh ), .SW(\指令信号生成器_1_sw ), .AND(\指令信号生成器_1_and ), .OR(\指令信号生成器_1_or ),
    .XOR(\指令信号生成器_1_xor ), .NOR(\指令信号生成器_1_nor ), .ANDI(\指令信号生成器_1_andi ), .ORI(\指令信号生成器_1_ori ),
    .XORI(\指令信号生成器_1_xori ), .LUI(\指令信号生成器_1_lui ), .SLL(\指令信号生成器_1_sll ), .SRL(\指令信号生成器_1_srl ),
    .SRA(\指令信号生成器_1_sra ), .SLLV(\指令信号生成器_1_sllv ), .SRLV(\指令信号生成器_1_srlv ), .SRAV(\指令信号生成器_1_srav ),
    .ALUSrc(ALUSrc), .RegSrc(RegSrc), .RegDst(RegDst), .RegWrite(RegWrite), .MemSrc(MemSrc), .MemDst(MemDst),
    .MemWrite(MemWrite), .BRANCH(BRANCH), .JUMP(JUMP), .ExtOp(ExtOp), .ALUCtr(ALUCtr), .CmpCtr(CmpCtr));
endmodule

module \指令信号生成器  (
  input  [5:0] OP,
  input  [5:0] FUNC,
  input  [4:0] RT,
  output ADD,
  output ADDU,
  output SUB,
  output SUBU,
  output ADDI,
  output ADDIU,
  output SLTI,
  output SLTIU,
  output SLT,
  output SLTU,
  output BEQ,
  output BNE,
  output BLEZ,
  output BGTZ,
  output BLTZ,
  output BGEZ,
  output BLTZAL,
  output BGEZAL,
  output J,
  output JAL,
  output JR,
  output JALR,
  output LB,
  output LH,
  output LW,
  output LBU,
  output LHU,
  output SB,
  output SH,
  output SW,
  output AND,
  output OR,
  output XOR,
  output NOR,
  output ANDI,
  output ORI,
  output XORI,
  output LUI,
  output SLL,
  output SRL,
  output SRA,
  output SLLV,
  output SRLV,
  output SRAV
);

  wire comparator_1_eq, comparator_2_eq, comparator_4_eq, comparator_5_eq, comparator_7_eq, comparator_8_eq,
       comparator_12_eq, comparator_13_eq, comparator_15_eq, comparator_16_eq, comparator_17_eq,
       comparator_18_eq, comparator_19_eq, comparator_20_eq, comparator_22_eq, comparator_23_eq,
       comparator_25_eq, comparator_26_eq, comparator_30_eq, comparator_31_eq, comparator_33_eq,
       comparator_34_eq, comparator_35_eq, comparator_36_eq, comparator_37_eq, comparator_38_eq,
       comparator_41_eq, comparator_42_eq, comparator_43_eq, comparator_44_eq, comparator_47_eq,
       comparator_48_eq, comparator_50_eq, comparator_51_eq, comparator_52_eq, comparator_53_eq,
       comparator_56_eq, comparator_57_eq, comparator_58_eq, comparator_59_eq, comparator_62_eq,
       comparator_63_eq, comparator_65_eq, comparator_66_eq;

  // Probe on 6'b100000
  // Probe on 6'b001000
  // Probe on 6'b101010
  // Probe on 6'b000100
  // Probe on 6'b000001
  // Probe on {5{1'b0}}
  // Probe on 6'b000010
  // Probe on 6'b100000
  // Probe on 6'b100101
  // Probe on 6'b100100
  // Probe on 6'b001100
  // Probe on {6{1'b0}}
  // Probe on 6'b000110
  Comparator #(.width(6)) comparator_1 (.a(OP), .b({6{1'b0}}), .eq(comparator_1_eq));  // open: gt, lt
  Comparator #(.width(6), .mode("unsigned")) comparator_2 (
    .a(FUNC), .b(6'b100000), .eq(comparator_2_eq));  // open: gt, lt
  Comparator #(.width(6), .mode("unsigned")) comparator_3 (.a(OP), .b(6'b001000), .eq(ADDI));  // open: gt, lt
  Comparator #(.width(6)) comparator_4 (.a(OP), .b({6{1'b0}}), .eq(comparator_4_eq));  // open: gt, lt
  Comparator #(.width(6), .mode("unsigned")) comparator_5 (
    .a(FUNC), .b(6'b101010), .eq(comparator_5_eq));  // open: gt, lt
  Comparator #(.width(6), .mode("unsigned")) comparator_6 (.a(OP), .b(6'b000100), .eq(BEQ));  // open: gt, lt
  Comparator #(.width(6)) comparator_7 (.a(OP), .b(6'b000001), .eq(comparator_7_eq));  // open: gt, lt
  Comparator #(.width(5), .mode("unsigned")) comparator_8 (
    .a(RT), .b({5{1'b0}}), .eq(comparator_8_eq));  // open: gt, lt
  Comparator #(.width(6), .mode("unsigned")) comparator_9 (.a(OP), .b(6'b000010), .eq(J));  // open: gt, lt
  Comparator #(.width(6), .mode("unsigned")) comparator_10 (.a(OP), .b(6'b100000), .eq(LB));  // open: gt, lt
  Comparator #(.width(6), .mode("unsigned")) comparator_11 (.a(OP), .b(6'b100101), .eq(LHU));  // open: gt, lt
  Comparator #(.width(6)) comparator_12 (.a(OP), .b({6{1'b0}}), .eq(comparator_12_eq));  // open: gt, lt
  Comparator #(.width(6), .mode("unsigned")) comparator_13 (
    .a(FUNC), .b(6'b100100), .eq(comparator_13_eq));  // open: gt, lt
  Comparator #(.width(6), .mode("unsigned")) comparator_14 (.a(OP), .b(6'b001100), .eq(ANDI));  // open: gt, lt
  Comparator #(.width(6)) comparator_15 (.a(OP), .b({6{1'b0}}), .eq(comparator_15_eq));  // open: gt, lt
  Comparator #(.width(6), .mode("unsigned")) comparator_16 (
    .a(FUNC), .b({6{1'b0}}), .eq(comparator_16_eq));  // open: gt, lt
  Comparator #(.width(6)) comparator_17 (.a(OP), .b({6{1'b0}}), .eq(comparator_17_eq));  // open: gt, lt
  Comparator #(.width(6), .mode("unsigned")) comparator_18 (
    .a(FUNC), .b(6'b000110), .eq(comparator_18_eq));  // open: gt, lt
  and and_1 (ADD, comparator_1_eq, comparator_2_eq);
  and and_2 (SLT, comparator_4_eq, comparator_5_eq);
  and and_3 (BLTZ, comparator_7_eq, comparator_8_eq);
  and and_4 (AND, comparator_12_eq, comparator_13_eq);
  and and_5 (SLL, comparator_15_eq, comparator_16_eq);
  and and_6 (SRLV, comparator_17_eq, comparator_18_eq);
  // Probe on 6'b100001
  // Probe on 6'b001001
  // Probe on 6'b101011
  // Probe on 6'b000101
  // Probe on 6'b000001
  // Probe on 5'b00001
  // Probe on 6'b000011
  // Probe on 6'b100001
  // Probe on 6'b101000
  // Probe on 6'b100101
  // Probe on 6'b001101
  // Probe on 6'b000010
  // Probe on 6'b000111
  Comparator #(.width(6)) comparator_19 (.a(OP), .b({6{1'b0}}), .eq(comparator_19_eq));  // open: gt, lt
  and and_7 (ADDU, comparator_19_eq, comparator_20_eq);
  Comparator #(.width(6), .mode("unsigned")) comparator_20 (
    .a(FUNC), .b(6'b100001), .eq(comparator_20_eq));  // open: gt, lt
  Comparator #(.width(6), .mode("unsigned")) comparator_21 (.a(OP), .b(6'b001001), .eq(ADDIU));  // open: gt, lt
  Comparator #(.width(6)) comparator_22 (.a(OP), .b({6{1'b0}}), .eq(comparator_22_eq));  // open: gt, lt
  and and_8 (SLTU, comparator_22_eq, comparator_23_eq);
  Comparator #(.width(6), .mode("unsigned")) comparator_23 (
    .a(FUNC), .b(6'b101011), .eq(comparator_23_eq));  // open: gt, lt
  Comparator #(.width(6), .mode("unsigned")) comparator_24 (.a(OP), .b(6'b000101), .eq(BNE));  // open: gt, lt
  Comparator #(.width(6)) comparator_25 (.a(OP), .b(6'b000001), .eq(comparator_25_eq));  // open: gt, lt
  and and_9 (BGEZ, comparator_25_eq, comparator_26_eq);
  Comparator #(.width(5), .mode("unsigned")) comparator_26 (
    .a(RT), .b(5'b00001), .eq(comparator_26_eq));  // open: gt, lt
  Comparator #(.width(6), .mode("unsigned")) comparator_27 (.a(OP), .b(6'b000011), .eq(JAL));  // open: gt, lt
  Comparator #(.width(6), .mode("unsigned")) comparator_28 (.a(OP), .b(6'b100001), .eq(LH));  // open: gt, lt
  Comparator #(.width(6), .mode("unsigned")) comparator_29 (.a(OP), .b(6'b101000), .eq(SB));  // open: gt, lt
  Comparator #(.width(6)) comparator_30 (.a(OP), .b({6{1'b0}}), .eq(comparator_30_eq));  // open: gt, lt
  and and_10 (OR, comparator_30_eq, comparator_31_eq);
  Comparator #(.width(6), .mode("unsigned")) comparator_31 (
    .a(FUNC), .b(6'b100101), .eq(comparator_31_eq));  // open: gt, lt
  Comparator #(.width(6), .mode("unsigned")) comparator_32 (.a(OP), .b(6'b001101), .eq(ORI));  // open: gt, lt
  Comparator #(.width(6)) comparator_33 (.a(OP), .b({6{1'b0}}), .eq(comparator_33_eq));  // open: gt, lt
  and and_11 (SRL, comparator_33_eq, comparator_34_eq);
  Comparator #(.width(6), .mode("unsigned")) comparator_34 (
    .a(FUNC), .b(6'b000010), .eq(comparator_34_eq));  // open: gt, lt
  Comparator #(.width(6)) comparator_35 (.a(OP), .b({6{1'b0}}), .eq(comparator_35_eq));  // open: gt, lt
  and and_12 (SRAV, comparator_35_eq, comparator_36_eq);
  Comparator #(.width(6), .mode("unsigned")) comparator_36 (
    .a(FUNC), .b(6'b000111), .eq(comparator_36_eq));  // open: gt, lt
  // Probe on 6'b100010
  // Probe on 6'b001010
  // Probe on 6'b000110
  // Probe on 6'b000001
  // Probe on 5'b10000
  // Probe on {6{1'b0}}
  // Probe on 6'b001000
  // Probe on 6'b100011
  // Probe on 6'b101001
  // Probe on 6'b100110
  // Probe on 6'b001110
  // Probe on 6'b000011
  Comparator #(.width(6)) comparator_37 (.a(OP), .b({6{1'b0}}), .eq(comparator_37_eq));  // open: gt, lt
  and and_13 (SUB, comparator_37_eq, comparator_38_eq);
  Comparator #(.width(6), .mode("unsigned")) comparator_38 (
    .a(FUNC), .b(6'b100010), .eq(comparator_38_eq));  // open: gt, lt
  Comparator #(.width(6), .mode("unsigned")) comparator_39 (.a(OP), .b(6'b001010), .eq(SLTI));  // open: gt, lt
  Comparator #(.width(6), .mode("unsigned")) comparator_40 (.a(OP), .b(6'b000110), .eq(BLEZ));  // open: gt, lt
  Comparator #(.width(6)) comparator_41 (.a(OP), .b(6'b000001), .eq(comparator_41_eq));  // open: gt, lt
  and and_14 (BLTZAL, comparator_41_eq, comparator_42_eq);
  Comparator #(.width(5), .mode("unsigned")) comparator_42 (
    .a(RT), .b(5'b10000), .eq(comparator_42_eq));  // open: gt, lt
  Comparator #(.width(6)) comparator_43 (.a(OP), .b({6{1'b0}}), .eq(comparator_43_eq));  // open: gt, lt
  and and_15 (JR, comparator_43_eq, comparator_44_eq);
  Comparator #(.width(6), .mode("unsigned")) comparator_44 (
    .a(FUNC), .b(6'b001000), .eq(comparator_44_eq));  // open: gt, lt
  Comparator #(.width(6), .mode("unsigned")) comparator_45 (.a(OP), .b(6'b100011), .eq(LW));  // open: gt, lt
  Comparator #(.width(6), .mode("unsigned")) comparator_46 (.a(OP), .b(6'b101001), .eq(SH));  // open: gt, lt
  Comparator #(.width(6)) comparator_47 (.a(OP), .b({6{1'b0}}), .eq(comparator_47_eq));  // open: gt, lt
  and and_16 (XOR, comparator_47_eq, comparator_48_eq);
  Comparator #(.width(6), .mode("unsigned")) comparator_48 (
    .a(FUNC), .b(6'b100110), .eq(comparator_48_eq));  // open: gt, lt
  Comparator #(.width(6), .mode("unsigned")) comparator_49 (.a(OP), .b(6'b001110), .eq(XORI));  // open: gt, lt
  Comparator #(.width(6)) comparator_50 (.a(OP), .b({6{1'b0}}), .eq(comparator_50_eq));  // open: gt, lt
  and and_17 (SRA, comparator_50_eq, comparator_51_eq);
  Comparator #(.width(6), .mode("unsigned")) comparator_51 (
    .a(FUNC), .b(6'b000011), .eq(comparator_51_eq));  // open: gt, lt
  // Probe on 6'b100011
  // Probe on 6'b001011
  // Probe on 6'b000111
  // Probe on 6'b000001
  // Probe on 5'b10001
  // Probe on {6{1'b0}}
  // Probe on 6'b001001
  // Probe on 6'b100100
  // Probe on 6'b101011
  // Probe on 6'b100111
  // Probe on 6'b001111
  // Probe on 6'b000100
  Comparator #(.width(6)) comparator_52 (.a(OP), .b({6{1'b0}}), .eq(comparator_52_eq));  // open: gt, lt
  Comparator #(.width(6), .mode("unsigned")) comparator_53 (
    .a(OP), .b(6'b100011), .eq(comparator_53_eq));  // open: gt, lt
  Comparator #(.width(6), .mode("unsigned")) comparator_54 (.a(OP), .b(6'b001011), .eq(SLTIU));  // open: gt, lt
  Comparator #(.width(6), .mode("unsigned")) comparator_55 (.a(OP), .b(6'b000111), .eq(BGTZ));  // open: gt, lt
  Comparator #(.width(6)) comparator_56 (.a(OP), .b(6'b000001), .eq(comparator_56_eq));  // open: gt, lt
  Comparator #(.width(5), .mode("unsigned")) comparator_57 (
    .a(RT), .b(5'b10001), .eq(comparator_57_eq));  // open: gt, lt
  Comparator #(.width(6)) comparator_58 (.a(OP), .b({6{1'b0}}), .eq(comparator_58_eq));  // open: gt, lt
  Comparator #(.width(6), .mode("unsigned")) comparator_59 (
    .a(FUNC), .b(6'b001001), .eq(comparator_59_eq));  // open: gt, lt
  Comparator #(.width(6), .mode("unsigned")) comparator_60 (.a(OP), .b(6'b100100), .eq(LBU));  // open: gt, lt
  Comparator #(.width(6), .mode("unsigned")) comparator_61 (.a(OP), .b(6'b101011), .eq(SW));  // open: gt, lt
  Comparator #(.width(6)) comparator_62 (.a(OP), .b({6{1'b0}}), .eq(comparator_62_eq));  // open: gt, lt
  Comparator #(.width(6), .mode("unsigned")) comparator_63 (
    .a(FUNC), .b(6'b100111), .eq(comparator_63_eq));  // open: gt, lt
  Comparator #(.width(6), .mode("unsigned")) comparator_64 (.a(OP), .b(6'b001111), .eq(LUI));  // open: gt, lt
  Comparator #(.width(6)) comparator_65 (.a(OP), .b({6{1'b0}}), .eq(comparator_65_eq));  // open: gt, lt
  Comparator #(.width(6), .mode("unsigned")) comparator_66 (
    .a(FUNC), .b(6'b000100), .eq(comparator_66_eq));  // open: gt, lt
  and and_18 (SUBU, comparator_52_eq, comparator_53_eq);
  and and_19 (BGEZAL, comparator_56_eq, comparator_57_eq);
  and and_20 (JALR, comparator_58_eq, comparator_59_eq);
  and and_21 (NOR, comparator_62_eq, comparator_63_eq);
  and and_22 (SLLV, comparator_65_eq, comparator_66_eq);
endmodule

module \控制信号生成器  (
  input  ADD,
  input  ADDU,
  input  SUB,
  input  SUBU,
  input  ADDI,
  input  ADDIU,
  input  SLTI,
  input  SLTIU,
  input  SLT,
  input  SLTU,
  input  BEQ,
  input  BNE,
  input  BLEZ,
  input  BGTZ,
  input  BLTZ,
  input  BGEZ,
  input  BLTZAL,
  input  BGEZAL,
  input  J,
  input  JAL,
  input  JR,
  input  JRAL,
  input  LB,
  input  LH,
  input  LW,
  input  LBU,
  input  LHU,
  input  SB,
  input  SH,
  input  SW,
  input  AND,
  input  OR,
  input  XOR,
  input  NOR,
  input  ANDI,
  input  ORI,
  input  XORI,
  input  LUI,
  input  SLL,
  input  SRL,
  input  SRA,
  input  SLLV,
  input  SRLV,
  input  SRAV,
  output [2:0] ALUSrc,
  output [1:0] RegSrc,
  output [1:0] RegDst,
  output RegWrite,
  output [1:0] MemSrc,
  output [2:0] MemDst,
  output MemWrite,
  output BRANCH,
  output [1:0] JUMP,
  output [1:0] ExtOp,
  output [3:0] ALUCtr,
  output [2:0] CmpCtr
);

  wire or_2_out, or_3_out, or_4_out, or_5_out, or_6_out, or_7_out, or_8_out, or_9_out, or_10_out, or_11_out,
       or_14_out, or_20_out, or_21_out, or_22_out, or_23_out, or_24_out, or_25_out, or_27_out,
       priority_encoder_1_gs, priority_encoder_2_gs, priority_encoder_3_gs;
  wire [1:0] multiplexer_3_out, multiplexer_6_out, multiplexer_8_out, priority_encoder_1_out;
  wire [2:0] priority_encoder_2_out, priority_encoder_3_out;
  wire [3:0] multiplexer_1_out, multiplexer_2_out, multiplexer_4_out, multiplexer_5_out, multiplexer_7_out,
       multiplexer_9_out, multiplexer_12_out, multiplexer_14_out, multiplexer_16_out, multiplexer_18_out;

  or or_1 (ALUSrc[2], BLTZ, BGEZ, BLTZAL, BGEZAL);
  Multiplexer #(.width(4)) multiplexer_1 (
    .in0(4'b1111), .in1(4'b1010), .out(multiplexer_1_out), .sel(or_2_out));  // open: en
  or or_2 (or_2_out, SLTU, SLTIU);
  or or_3 (or_3_out, SLT, SLTI);
  Multiplexer #(.width(4)) multiplexer_2 (
    .in0(multiplexer_1_out), .in1(4'b1001), .out(multiplexer_2_out), .sel(or_3_out));  // open: en
  or or_4 (or_4_out, SRA, SRAV);
  Multiplexer #(.width(2)) multiplexer_3 (
    .in0(2'b11), .in1(2'b10), .out(multiplexer_3_out), .sel(or_5_out));  // open: en
  buf or_5 (or_5_out, LUI);  // OR_Gate
  Multiplexer #(.width(4)) multiplexer_4 (
    .in0(multiplexer_2_out), .in1(4'b1000), .out(multiplexer_4_out), .sel(or_4_out));  // open: en
  Multiplexer #(.width(4)) multiplexer_5 (
    .in0(multiplexer_4_out), .in1(4'b0111), .out(multiplexer_5_out), .sel(or_6_out));  // open: en
  or or_6 (or_6_out, SRL, SRLV);
  Multiplexer #(.width(2)) multiplexer_6 (
    .in0(2'b00), .in1(2'b01), .out(multiplexer_6_out), .sel(or_7_out));  // open: en
  or or_7 (or_7_out, ADD, ADDU, SUB, SUBU, SLT, SLTU, AND, OR, XOR, NOR, SLL, SRL, SRA, SLLV, SRLV, SRAV);
  or or_8 (or_8_out, LB, LH, LW, LBU, LHU, SB, SH, SW);
  Multiplexer #(.width(4)) multiplexer_7 (
    .in0(multiplexer_5_out), .in1(4'b0110), .out(multiplexer_7_out), .sel(or_9_out));  // open: en
  or or_9 (or_9_out, SLL, SLLV);
  or or_10 (or_10_out, BLTZ, BLTZAL);
  or or_11 (or_11_out, BGEZ, BGEZAL);
  Priority_Encoder #(.select(2)) priority_encoder_1 (
    .in0(SB), .in1(SH), .in2(SW), .out(priority_encoder_1_out), .gs(priority_encoder_1_gs));  // open: in3, en_out, en_in
  or or_12 (JUMP[0], J, JAL, JR, JRAL);
  or or_13 (JUMP[1], JRAL, JR);
  Multiplexer #(.width(2)) multiplexer_8 (
    .in0(multiplexer_3_out), .in1(2'b01), .out(multiplexer_8_out), .sel(or_8_out));  // open: en
  Multiplexer #(.width(4)) multiplexer_9 (
    .in0(multiplexer_7_out), .in1(4'b0101), .out(multiplexer_9_out), .sel(or_14_out));  // open: en
  buf or_14 (or_14_out, NOR);  // OR_Gate
  Priority_Encoder priority_encoder_2 (
    .in0(BEQ), .in1(BNE), .in2(BLEZ), .in3(BGTZ), .in4(or_10_out), .in5(or_11_out), .in6(1'b0), .in7(1'b0),
    .out(priority_encoder_2_out), .gs(priority_encoder_2_gs));  // open: en_in, en_out
  or or_15 (ALUSrc[1], ADDI, ADDIU, SLTI, SLTIU, LB, LH, LW, LBU, LHU, SB, SH, SW, ANDI, ORI, XORI, LUI);
  or or_16 (RegSrc[0], LW, LB, LH, LBU, LHU);
  or or_17 (RegSrc[1], BLTZAL, JAL, JRAL, BGEZAL);
  nor nor_1 (RegWrite, BEQ, BNE, BLEZ, BGTZ, BLTZ, BGEZ, J, JR, SW, SH, SB);
  Multiplexer #(.width(2)) multiplexer_10 (
    .in0(2'b11), .in1(priority_encoder_1_out), .out(MemSrc), .sel(priority_encoder_1_gs));  // open: en
  or or_18 (MemWrite, SW, SB, SH);
  or or_19 (BRANCH, BEQ, BNE, BLEZ, BGTZ, BLTZ, BGEZ, BLTZAL, BGEZAL);
  Multiplexer #(.width(2)) multiplexer_11 (
    .in0(multiplexer_8_out), .in1(2'b00), .out(ExtOp), .sel(or_20_out));  // open: en
  or or_20 (or_20_out, ORI, ANDI, XORI, ADDI, ADDIU, SLTI, SLTIU);
  Multiplexer #(.width(4)) multiplexer_12 (
    .in0(multiplexer_9_out), .in1(4'b0100), .out(multiplexer_12_out), .sel(or_21_out));  // open: en
  or or_21 (or_21_out, XOR, XORI);
  Multiplexer #(.width(3)) multiplexer_13 (
    .in0(3'b111), .in1(priority_encoder_2_out), .out(CmpCtr), .sel(priority_encoder_2_gs));  // open: en
  Multiplexer #(.width(4)) multiplexer_14 (
    .in0(multiplexer_12_out), .in1(4'b0011), .out(multiplexer_14_out), .sel(or_22_out));  // open: en
  or or_22 (or_22_out, ORI, OR, LUI);
  Multiplexer #(.width(2)) multiplexer_15 (
    .in0(multiplexer_6_out), .in1(2'b10), .out(RegDst), .sel(or_23_out));  // open: en
  or or_23 (or_23_out, BLTZAL, JAL, JRAL, BGEZAL);
  Priority_Encoder priority_encoder_3 (
    .in0(LB), .in1(LH), .in2(LW), .in3(LBU), .in4(LHU), .out(priority_encoder_3_out),
    .gs(priority_encoder_3_gs));  // open: in5, in6, in7, en_in, en_out
  Multiplexer #(.width(4)) multiplexer_16 (
    .in0(multiplexer_14_out), .in1(4'b0010), .out(multiplexer_16_out), .sel(or_24_out));  // open: en
  or or_24 (or_24_out, AND, ANDI);
  or or_25 (or_25_out, SUB, SUBU);
  or or_26 (ALUSrc[0], SLL, SRL, SRA);
  Multiplexer #(.width(3)) multiplexer_17 (
    .in0(3'b111), .in1(priority_encoder_3_out), .out(MemDst), .sel(priority_encoder_3_gs));  // open: en
  Multiplexer #(.width(4)) multiplexer_18 (
    .in0(multiplexer_16_out), .in1(4'b0001), .out(multiplexer_18_out), .sel(or_25_out));  // open: en
  or or_27 (or_27_out, ADD, ADDU, ADDI, ADDIU, LB, LH, LW, LBU, LHU, SB, SH, SW);
  Multiplexer #(.width(4)) multiplexer_19 (
    .in0(multiplexer_18_out), .in1(4'b0000), .out(ALUCtr), .sel(or_27_out));  // open: en
endmodule
