// Logisim project weak.circ as structural Verilog: 14 circuits, main circuit MIPS
module main (
  input  reset,
  output [31:0] Instr,
  output [31:0] pc,
  output RegWrite,
  output [4:0] RegAddr,
  output [31:0] RegData,
  output MemWrite,
  output [31:0] MemAddr,
  output [31:0] MemData
);

  wire clock_1_out;

  Clock clock_1 (.out(clock_1_out));
  // Probe on Instr
  MIPS mips_1 (
    .CLK(clock_1_out), .RESET(reset), .out_3(Instr), .out_4(pc), .out_5(RegWrite), .out_6(RegAddr),
    .out_7(RegData), .out_8(MemWrite), .out_9(MemAddr), .out_10(MemData));
endmodule

module MIPS (
  input  CLK,
  input  RESET,
  output [31:0] out_3,
  output [31:0] out_4,
  output out_5,
  output [4:0] out_6,
  output [31:0] out_7,
  output out_8,
  output [31:0] out_9,
  output [31:0] out_10
);

  wire alu_src, and_1_out, comparator_1_eq, mem_to_reg, next_pc_sel, reg_dst;
  wire [1:0] ext_op;
  wire [2:0] alu_ctr;
  wire [15:0] shifter_1_out;
  wire [31:0] adder_1_out, adder_2_out, adder_3_out, bit_extender_1_out, ext_1_result, mem_data,
       multiplexer_1_out, multiplexer_2_out, reg_data1;

  Shifter #(.width(16)) shifter_1 (.in(out_3[15:0]), .\dist (4'b0010), .out(shifter_1_out));
  // Probe on out_4
  // Probe on out_3
  // Probe on ext_op
  // Probe on alu_ctr
  Adder #(.width(32)) adder_1 (.a(out_4), .b(32'h4), .out(adder_1_out));  // open: cin, cout
  assign bit_extender_1_out = {{16{shifter_1_out[15]}}, shifter_1_out};  // Bit_Extender bit_extender_1
  Multiplexer #(.width(32)) multiplexer_1 (
    .in0(out_10), .in1(ext_1_result), .out(multiplexer_1_out), .sel(alu_src));  // open: en
  EXT ext_1 (.OPRD(out_3[15:0]), .OP(ext_op), .RESULT(ext_1_result));
  Adder #(.width(32)) adder_2 (.a(out_4), .b(32'h4), .out(adder_2_out));  // open: cin, cout
  and and_1 (and_1_out, next_pc_sel, comparator_1_eq);
  Adder #(.width(32)) adder_3 (.a(adder_1_out), .b(bit_extender_1_out), .out(adder_3_out));  // open: cin, cout
  // Probe on out_3[25:21]
  // Probe on out_3[20:16]
  // Probe on out_3[15:11]
  IFU ifu_1 (.CLK(CLK), .RESET(RESET), .NEXT_PC(multiplexer_2_out), .PC(out_4), .INSTR(out_3));
  Multiplexer #(.width(32)) multiplexer_2 (
    .in0(adder_2_out), .in1(adder_3_out), .out(multiplexer_2_out), .sel(and_1_out));  // open: en
  // Probe on multiplexer_2_out
  Comparator #(.width(32), .mode("unsigned")) comparator_1 (
    .a(out_9), .b({32{1'b0}}), .eq(comparator_1_eq));  // open: gt, lt
  ALU alu_1 (.OPRD1(reg_data1), .OPRD2(multiplexer_1_out), .OP(alu_ctr), .RESULT(out_9));
  // Probe on out_3[15:0]
  // Probe on out_3[15:0]
  // Probe on out_3[15:0]
  // Probe on reg_data1
  // Probe on reg_data1
  // Probe on reg_data1
  Controller controller_1 (
    .OP(out_3[31:26]), .FUNC(out_3[5:0]), .RegDst(reg_dst), .ALUSrc(alu_src), .MemToReg(mem_to_reg),
    .RegWrite(out_5), .MemWrite(out_8), .NEXT_PC_SEL(next_pc_sel), .ExtOp(ext_op), .ALUCtr(alu_ctr));
  // Probe on out_9
  // Probe on out_9
  // Probe on out_9
  // Probe on out_10
  // Probe on out_10
  // Probe on out_10
  Multiplexer #(.width(5)) multiplexer_3 (
    .in0(out_3[20:16]), .in1(out_3[15:11]), .out(out_6), .sel(reg_dst));  // open: en
  Multiplexer #(.width(32)) multiplexer_4 (.in0(out_9), .in1(mem_data), .out(out_7), .sel(mem_to_reg));  // open: en
  DM dm_1 (.CLK(CLK), .RESET(RESET), .WE(out_8), .ADDR(out_9), .WD(out_10), .RD(mem_data));
  // Probe on mem_data
  // Probe on mem_data
  // Probe on mem_data
  GRF grf_1 (
    .RA1(out_3[25:21]), .RA2(out_3[20:16]), .WA(out_6), .WD(out_7), .clk(CLK), .reset(RESET), .WE(out_5),
    .RD1(reg_data1), .RD2(out_10));

  // Other names for the same wires on the sheet: alu_result[31:0] = out_9; func[5:0] = out_3[5:0];
  //   imm_off[15:0] = out_3[15:0]; instr[31:0] = out_3; else[4:0] = out_3[10:6]; rd[4:0] = out_3[15:11];
  //   rt[4:0] = out_3[20:16]; rs[4:0] = out_3[25:21]; op[5:0] = out_3[31:26]; mem_write = out_8; pc[31:0] = out_4;
  //   reg_addr[4:0] = out_6; reg_data[31:0] = out_7; reg_data2[31:0] = out_10; reg_write = out_5
endmodule

module IFU (
  input  CLK,
  input  RESET,
  input  [31:0] NEXT_PC,
  output [31:0] PC,
  output [31:0] INSTR
);

  // Probe on PC
  PC u_PC (.CLK(CLK), .RESET(RESET), .NEXT(NEXT_PC), .ADDR(PC));
  IM IM (.ADDR(PC), .DATA(INSTR));
  // Probe on INSTR

  // Other names for the same wires on the sheet: addr[31:0] = NEXT_PC
endmodule

module PC (
  input  CLK,
  input  RESET,
  input  [31:0] NEXT,
  output [31:0] ADDR
);

  \_32位带范围异步复位寄存器  \u_32位带范围异步复位寄存器_1  (.CLK(CLK), .RESET(RESET), .MIN(32'h3000), .MAX(32'h6fff), .D(NEXT), .Q(ADDR));
  // Probe on ADDR
endmodule

module \_32位带范围异步复位寄存器  (
  input  CLK,
  input  RESET,
  input  [31:0] MIN,
  input  [31:0] MAX,
  input  [31:0] D,
  output [31:0] Q
);

  wire comparator_1_gt;
  wire [31:0] multiplexer_1_out, register_1_q, xor_1_out, xor_2_out;

  assign xor_1_out = MIN ^ D;  // XOR_Gate xor_1, 32 bits wide
  assign xor_2_out = MIN ^ MIN;  // XOR_Gate xor_2, 32 bits wide
  Comparator #(.width(32), .mode("unsigned")) comparator_1 (.a(D), .b(MAX), .gt(comparator_1_gt));  // open: eq, lt
  Multiplexer #(.width(32)) multiplexer_1 (
    .in0(xor_1_out), .in1(xor_2_out), .out(multiplexer_1_out), .sel(comparator_1_gt));  // open: en
  Register #(.width(32)) register_1 (.D(multiplexer_1_out), .Q(register_1_q), .clk(CLK), .clr(RESET));  // open: en
  assign Q = MIN ^ register_1_q;  // XOR_Gate xor_3, 32 bits wide
endmodule

module IM (
  input  [31:0] ADDR,
  output [31:0] DATA
);

  wire [31:0] shifter_1_out, subtractor_1_out;

  // Probe on ADDR
  Subtractor #(.width(32)) subtractor_1 (.a(ADDR), .b(32'h3000), .out(subtractor_1_out));  // open: bin, bout
  Shifter #(.width(32), .shift("lr")) shifter_1 (.in(subtractor_1_out), .\dist (5'b00010), .out(shifter_1_out));
  ROM #(.addrWidth(12), .dataWidth(32)) rom_1 (.addr(shifter_1_out[11:0]), .data(DATA));  // open: sel
  // Probe on DATA

  // Notes on the sheet:
  //   contents of rom_1 (hex, n*v repeats v):
  //   341c0000 341d0000 34013456 210820 8c010004 ac010004 3c027878 411822 3c051234 34040005 0 ac85ffff
  //   8c83ffff 10650001 1000000d 34670404 10e3000b 0 3c087777 3508ffff 80022 34001100 e65020 34080000
  //   34090001 340a0001 10a4020 1109fffe 1000ffff
endmodule

module GRF (
  input  clk,
  input  reset,
  input  WE,
  input  [4:0] RA1,
  input  [4:0] RA2,
  input  [4:0] WA,
  input  [31:0] WD,
  output [31:0] RD1,
  output [31:0] RD2
);

  wire and_1_out, and_2_out, and_3_out, and_4_out, and_5_out, and_6_out, and_7_out, and_8_out, and_9_out,
       and_10_out, and_11_out, and_12_out, and_13_out, and_14_out, and_15_out, and_16_out, and_17_out,
       and_18_out, and_19_out, and_20_out, and_21_out, and_22_out, and_23_out, and_24_out, and_25_out,
       and_26_out, and_27_out, and_28_out, and_29_out, and_30_out, and_31_out, and_32_out, WE0, WE1, WE2,
       WE3, WE4, WE5, WE6, WE7, WE8, WE9, WE10, WE11, WE12, WE13, WE14, WE15, WE16, WE17, WE18, WE19, WE20,
       WE21, WE22, WE23, WE24, WE25, WE26, WE27, WE28, WE29, WE30, WE31;
  wire [31:0] D0, D1, D2, D3, D4, D5, D6, D7, D8, D9, D10, D11, D12, D13, D14, D15, D16, D17, D18, D19, D20,
       D21, D22, D23, D24, D25, D26, D27, D28, D29, D30, D31;

  Decoder #(.select(5)) decoder_1 (
    .out0(WE0), .out1(WE1), .out2(WE2), .out3(WE3), .out4(WE4), .out5(WE5), .out6(WE6), .out7(WE7),
    .out8(WE8), .out9(WE9), .out10(WE10), .out11(WE11), .out12(WE12), .out13(WE13), .out14(WE14),
    .out15(WE15), .out16(WE16), .out17(WE17), .out18(WE18), .out19(WE19), .out20(WE20), .out21(WE21),
    .out22(WE22), .out23(WE23), .out24(WE24), .out25(WE25), .out26(WE26), .out27(WE27), .out28(WE28),
    .out29(WE29), .out30(WE30), .out31(WE31), .sel(WA));  // open: en
  and and_1 (and_1_out, WE, WE0);
  and and_2 (and_2_out, WE, WE1);
  and and_3 (and_3_out, WE, WE2);
  and and_4 (and_4_out, WE, WE3);
  and and_5 (and_5_out, WE, WE4);
  and and_6 (and_6_out, WE, WE5);
  and and_7 (and_7_out, WE, WE6);
  and and_8 (and_8_out, WE, WE7);
  \_32位带使能异步复位寄存器  \u_32位带使能异步复位寄存器_1  (.CLK(clk), .RESET(reset), .EN(and_1_out), .D({32{1'b0}}), .Q(D0));
  \_32位带使能异步复位寄存器  \u_32位带使能异步复位寄存器_2  (.CLK(clk), .RESET(reset), .EN(and_2_out), .D(WD), .Q(D1));
  \_32位带使能异步复位寄存器  \u_32位带使能异步复位寄存器_3  (.CLK(clk), .RESET(reset), .EN(and_3_out), .D(WD), .Q(D2));
  \_32位带使能异步复位寄存器  \u_32位带使能异步复位寄存器_4  (.CLK(clk), .RESET(reset), .EN(and_4_out), .D(WD), .Q(D3));
  \_32位带使能异步复位寄存器  \u_32位带使能异步复位寄存器_5  (.CLK(clk), .RESET(reset), .EN(and_5_out), .D(WD), .Q(D4));
  \_32位带使能异步复位寄存器  \u_32位带使能异步复位寄存器_6  (.CLK(clk), .RESET(reset), .EN(and_6_out), .D(WD), .Q(D5));
  \_32位带使能异步复位寄存器  \u_32位带使能异步复位寄存器_7  (.CLK(clk), .RESET(reset), .EN(and_7_out), .D(WD), .Q(D6));
  \_32位带使能异步复位寄存器  \u_32位带使能异步复位寄存器_8  (.CLK(clk), .RESET(reset), .EN(and_8_out), .D(WD), .Q(D7));
  and and_9 (and_9_out, WE, WE8);
  and and_10 (and_10_out, WE, WE9);
  and and_11 (and_11_out, WE, WE10);
  and and_12 (and_12_out, WE, WE11);
  and and_13 (and_13_out, WE, WE12);
  and and_14 (and_14_out, WE, WE13);
  and and_15 (and_15_out, WE, WE14);
  and and_16 (and_16_out, WE, WE15);
  \_32位带使能异步复位寄存器  \u_32位带使能异步复位寄存器_9  (.CLK(clk), .RESET(reset), .EN(and_9_out), .D(WD), .Q(D8));
  \_32位带使能异步复位寄存器  \u_32位带使能异步复位寄存器_10  (.CLK(clk), .RESET(reset), .EN(and_10_out), .D(WD), .Q(D9));
  \_32位带使能异步复位寄存器  \u_32位带使能异步复位寄存器_11  (.CLK(clk), .RESET(reset), .EN(and_11_out), .D(WD), .Q(D10));
  \_32位带使能异步复位寄存器  \u_32位带使能异步复位寄存器_12  (.CLK(clk), .RESET(reset), .EN(and_12_out), .D(WD), .Q(D11));
  \_32位带使能异步复位寄存器  \u_32位带使能异步复位寄存器_13  (.CLK(clk), .RESET(reset), .EN(and_13_out), .D(WD), .Q(D12));
  \_32位带使能异步复位寄存器  \u_32位带使能异步复位寄存器_14  (.CLK(clk), .RESET(reset), .EN(and_14_out), .D(WD), .Q(D13));
  \_32位带使能异步复位寄存器  \u_32位带使能异步复位寄存器_15  (.CLK(clk), .RESET(reset), .EN(and_15_out), .D(WD), .Q(D14));
  \_32位带使能异步复位寄存器  \u_32位带使能异步复位寄存器_16  (.CLK(clk), .RESET(reset), .EN(and_16_out), .D(WD), .Q(D15));
  Multiplexer #(.select(5), .width(32)) multiplexer_1 (
    .in0(D0), .in1(D1), .in2(D2), .in3(D3), .in4(D4), .in5(D5), .in6(D6), .in7(D7), .in8(D8), .in9(D9),
    .in10(D10), .in11(D11), .in12(D12), .in13(D13), .in14(D14), .in15(D15), .in16(D16), .in17(D17),
    .in18(D18), .in19(D19), .in20(D20), .in21(D21), .in22(D22), .in23(D23), .in24(D24), .in25(D25),
    .in26(D26), .in27(D27), .in28(D28), .in29(D29), .in30(D30), .in31(D31), .out(RD1), .sel(RA1));  // open: en
  and and_17 (and_17_out, WE, WE16);
  and and_18 (and_18_out, WE, WE17);
  and and_19 (and_19_out, WE, WE18);
  and and_20 (and_20_out, WE, WE19);
  and and_21 (and_21_out, WE, WE20);
  and and_22 (and_22_out, WE, WE21);
  and and_23 (and_23_out, WE, WE22);
  and and_24 (and_24_out, WE, WE23);
  \_32位带使能异步复位寄存器  \u_32位带使能异步复位寄存器_17  (.CLK(clk), .RESET(reset), .EN(and_17_out), .D(WD), .Q(D16));
  \_32位带使能异步复位寄存器  \u_32位带使能异步复位寄存器_18  (.CLK(clk), .RESET(reset), .EN(and_18_out), .D(WD), .Q(D17));
  \_32位带使能异步复位寄存器  \u_32位带使能异步复位寄存器_19  (.CLK(clk), .RESET(reset), .EN(and_19_out), .D(WD), .Q(D18));
  \_32位带使能异步复位寄存器  \u_32位带使能异步复位寄存器_20  (.CLK(clk), .RESET(reset), .EN(and_20_out), .D(WD), .Q(D19));
  \_32位带使能异步复位寄存器  \u_32位带使能异步复位寄存器_21  (.CLK(clk), .RESET(reset), .EN(and_21_out), .D(WD), .Q(D20));
  \_32位带使能异步复位寄存器  \u_32位带使能异步复位寄存器_22  (.CLK(clk), .RESET(reset), .EN(and_22_out), .D(WD), .Q(D21));
  \_32位带使能异步复位寄存器  \u_32位带使能异步复位寄存器_23  (.CLK(clk), .RESET(reset), .EN(and_23_out), .D(WD), .Q(D22));
  \_32位带使能异步复位寄存器  \u_32位带使能异步复位寄存器_24  (.CLK(clk), .RESET(reset), .EN(and_24_out), .D(WD), .Q(D23));
  and and_25 (and_25_out, WE, WE24);
  and and_26 (and_26_out, WE, WE25);
  and and_27 (and_27_out, WE, WE26);
  and and_28 (and_28_out, WE, WE27);
  and and_29 (and_29_out, WE, WE28);
  and and_30 (and_30_out, WE, WE29);
  and and_31 (and_31_out, WE, WE30);
  and and_32 (and_32_out, WE, WE31);
  \_32位带使能异步复位寄存器  \u_32位带使能异步复位寄存器_25  (.CLK(clk), .RESET(reset), .EN(and_25_out), .D(WD), .Q(D24));
  \_32位带使能异步复位寄存器  \u_32位带使能异步复位寄存器_26  (.CLK(clk), .RESET(reset), .EN(and_26_out), .D(WD), .Q(D25));
  \_32位带使能异步复位寄存器  \u_32位带使能异步复位寄存器_27  (.CLK(clk), .RESET(reset), .EN(and_27_out), .D(WD), .Q(D26));
  \_32位带使能异步复位寄存器  \u_32位带使能异步复位寄存器_28  (.CLK(clk), .RESET(reset), .EN(and_28_out), .D(WD), .Q(D27));
  \_32位带使能异步复位寄存器  \u_32位带使能异步复位寄存器_29  (.CLK(clk), .RESET(reset), .EN(and_29_out), .D(WD), .Q(D28));
  \_32位带使能异步复位寄存器  \u_32位带使能异步复位寄存器_30  (.CLK(clk), .RESET(reset), .EN(and_30_out), .D(WD), .Q(D29));
  \_32位带使能异步复位寄存器  \u_32位带使能异步复位寄存器_31  (.CLK(clk), .RESET(reset), .EN(and_31_out), .D(WD), .Q(D30));
  \_32位带使能异步复位寄存器  \u_32位带使能异步复位寄存器_32  (.CLK(clk), .RESET(reset), .EN(and_32_out), .D(WD), .Q(D31));
  Multiplexer #(.select(5), .width(32)) multiplexer_2 (
    .in0(D0), .in1(D1), .in2(D2), .in3(D3), .in4(D4), .in5(D5), .in6(D6), .in7(D7), .in8(D8), .in9(D9),
    .in10(D10), .in11(D11), .in12(D12), .in13(D13), .in14(D14), .in15(D15), .in16(D16), .in17(D17),
    .in18(D18), .in19(D19), .in20(D20), .in21(D21), .in22(D22), .in23(D23), .in24(D24), .in25(D25),
    .in26(D26), .in27(D27), .in28(D28), .in29(D29), .in30(D30), .in31(D31), .out(RD2), .sel(RA2));  // open: en

  // Other names for the same wires on the sheet: A1[4:0] = RA1; A2[4:0] = RA2; A3[4:0] = WA
endmodule

module \_32位带使能异步复位寄存器  (
  input  CLK,
  input  RESET,
  input  EN,
  input  [31:0] D,
  output [31:0] Q
);

  Register #(.width(32)) register_1 (.D(D), .en(EN), .Q(Q), .clk(CLK), .clr(RESET));
endmodule

module ALU (
  input  [31:0] OPRD1,
  input  [31:0] OPRD2,
  input  [2:0] OP,
  output [31:0] RESULT
);

  wire comparator_1_eq, comparator_1_gt, comparator_1_lt;
  wire [31:0] adder_1_out, bit_extender_1_out, bit_extender_2_out, bit_extender_3_out, or_1_out,
       subtractor_1_out;

  Adder #(.width(32)) adder_1 (.a(OPRD1), .b(OPRD2), .out(adder_1_out));  // open: cin, cout
  Subtractor #(.width(32)) subtractor_1 (.a(OPRD1), .b(OPRD2), .out(subtractor_1_out));  // open: bin, bout
  assign or_1_out = OPRD1 | OPRD2;  // OR_Gate or_1, 32 bits wide
  Comparator #(.width(32), .mode("unsigned")) comparator_1 (
    .a(OPRD1), .b(OPRD2), .gt(comparator_1_gt), .eq(comparator_1_eq), .lt(comparator_1_lt));
  assign bit_extender_1_out = {{31{1'b0}}, comparator_1_gt};  // Bit_Extender bit_extender_1
  assign bit_extender_2_out = {{31{1'b0}}, comparator_1_eq};  // Bit_Extender bit_extender_2
  assign bit_extender_3_out = {{31{1'b0}}, comparator_1_lt};  // Bit_Extender bit_extender_3
  Multiplexer #(.select(3), .width(32)) multiplexer_1 (
    .in0(adder_1_out), .in1(subtractor_1_out), .in2(or_1_out), .in3(bit_extender_1_out),
    .in4(bit_extender_2_out), .in5(bit_extender_3_out), .out(RESULT), .sel(OP));  // open: in6, in7, en
  // Probe on RESULT
endmodule

module DM (
  input  CLK,
  input  RESET,
  input  WE,
  input  [31:0] ADDR,
  input  [31:0] WD,
  output [31:0] RD
);

  wire [31:0] shifter_1_out;

  // Probe on ADDR
  // Probe on WD
  Shifter #(.width(32), .shift("lr")) shifter_1 (.in(ADDR), .\dist (5'b00010), .out(shifter_1_out));
  RAM #(.addrWidth(12), .dataWidth(32), .bus("separate")) ram_1 (
    .addr(shifter_1_out[11:0]), .din(WD), .data(RD), .str(WE), .clk(CLK), .clr(RESET));  // open: sel, ld
  // Probe on RD
endmodule

module EXT (
  input  [15:0] OPRD,
  input  [1:0] OP,
  output [31:0] RESULT
);

  wire [31:0] bit_extender_1_out, bit_extender_2_out, bit_extender_3_out, shifter_1_out;

  // Probe on OPRD
  assign bit_extender_1_out = {{16{1'b0}}, OPRD};  // Bit_Extender bit_extender_1
  assign bit_extender_2_out = {{16{OPRD[15]}}, OPRD};  // Bit_Extender bit_extender_2
  assign bit_extender_3_out = {{16{OPRD[15]}}, OPRD};  // Bit_Extender bit_extender_3
  Shifter #(.width(32)) shifter_1 (.in(bit_extender_3_out), .\dist (5'b00010), .out(shifter_1_out));
  Multiplexer #(.select(2), .width(32)) multiplexer_1 (
    .in0(bit_extender_1_out), .in1(bit_extender_2_out), .in2({OPRD, {16{1'b0}}}), .in3(shifter_1_out),
    .out(RESULT), .sel(OP));  // open: en
  // Probe on RESULT
endmodule

module Controller (
  input  [5:0] OP,
  input  [5:0] FUNC,
  output RegDst,
  output ALUSrc,
  output MemToReg,
  output RegWrite,
  output MemWrite,
  output NEXT_PC_SEL,
  output [1:0] ExtOp,
  output [2:0] ALUCtr
);

  wire \指令信号生成器_1_add , \指令信号生成器_1_beq , \指令信号生成器_1_lui , \指令信号生成器_1_lw , \指令信号生成器_1_ori , \指令信号生成器_1_sub ,
       \指令信号生成器_1_sw ;

  \指令信号生成器  \u_指令信号生成器_1  (
    .OP(OP), .FUNC(FUNC), .ADD(\指令信号生成器_1_add ), .SUB(\指令信号生成器_1_sub ), .ORI(\指令信号生成器_1_ori ),
    .LW(\指令信号生成器_1_lw ), .SW(\指令信号生成器_1_sw ), .BEQ(\指令信号生成器_1_beq ), .LUI(\指令信号生成器_1_lui ));
  \控制信号生成器  \u_控制信号生成器_1  (
    .ADD(\指令信号生成器_1_add ), .SUB(\指令信号生成器_1_sub ), .ORI(\指令信号生成器_1_ori ), .LW(\指令信号生成器_1_lw ),
    .SW(\指令信号生成器_1_sw ), .BEQ(\指令信号生成器_1_beq ), .LUI(\指令信号生成器_1_lui ), .RegDst(RegDst), .ALUSrc(ALUSrc),
    .MemToReg(MemToReg), .RegWrite(RegWrite), .MemWrite(MemWrite), .NEXT_PC_SEL(NEXT_PC_SEL), .ExtOp(ExtOp),
    .ALUCtr(ALUCtr));
endmodule

module \指令信号生成器  (
  input  [5:0] OP,
  input  [5:0] FUNC,
  output ADD,
  output SUB,
  output ORI,
  output LW,
  output SW,
  output BEQ,
  output LUI
);

  // Probe on 6'b100000
  // Probe on 6'b100010
  // Probe on 6'b001101
  // Probe on 6'b100011
  // Probe on 6'b101011
  // Probe on 6'b000100
  // Probe on 6'b001111
  Comparator #(.width(6), .mode("unsigned")) comparator_1 (.a(FUNC), .b(6'b100000), .eq(ADD));  // open: gt, lt
  Comparator #(.width(6), .mode("unsigned")) comparator_2 (.a(FUNC), .b(6'b100010), .eq(SUB));  // open: gt, lt
  Comparator #(.width(6), .mode("unsigned")) comparator_3 (.a(OP), .b(6'b001101), .eq(ORI));  // open: gt, lt
  Comparator #(.width(6), .mode("unsigned")) comparator_4 (.a(OP), .b(6'b100011), .eq(LW));  // open: gt, lt
  Comparator #(.width(6), .mode("unsigned")) comparator_5 (.a(OP), .b(6'b101011), .eq(SW));  // open: gt, lt
  Comparator #(.width(6), .mode("unsigned")) comparator_6 (.a(OP), .b(6'b000100), .eq(BEQ));  // open: gt, lt
  Comparator #(.width(6), .mode("unsigned")) comparator_7 (.a(OP), .b(6'b001111), .eq(LUI));  // open: gt, lt
endmodule

module \控制信号生成器  (
  input  ADD,
  input  SUB,
  input  ORI,
  input  LW,
  input  SW,
  input  BEQ,
  input  LUI,
  output RegDst,
  output ALUSrc,
  output MemToReg,
  output RegWrite,
  output MemWrite,
  output NEXT_PC_SEL,
  output [1:0] ExtOp,
  output [2:0] ALUCtr
);

  wire or_1_out, or_2_out, or_3_out, or_4_out, or_5_out, or_6_out, or_13_out, or_14_out;
  wire [1:0] multiplexer_3_out, multiplexer_5_out;
  wire [2:0] multiplexer_1_out, multiplexer_2_out, multiplexer_4_out, multiplexer_6_out;

  Multiplexer #(.width(3)) multiplexer_1 (
    .in0(3'b101), .in1(3'b100), .out(multiplexer_1_out), .sel(or_1_out));  // open: en
  buf or_1 (or_1_out, 1'b0);  // OR_Gate
  Multiplexer #(.width(3)) multiplexer_2 (
    .in0(multiplexer_1_out), .in1(3'b011), .out(multiplexer_2_out), .sel(or_2_out));  // open: en
  buf or_2 (or_2_out, 1'b0);  // OR_Gate
  Multiplexer #(.width(2)) multiplexer_3 (
    .in0(2'b11), .in1(2'b10), .out(multiplexer_3_out), .sel(or_3_out));  // open: en
  buf or_3 (or_3_out, LUI);  // OR_Gate
  Multiplexer #(.width(3)) multiplexer_4 (
    .in0(multiplexer_2_out), .in1(3'b010), .out(multiplexer_4_out), .sel(or_4_out));  // open: en
  or or_4 (or_4_out, ORI, LUI);
  Multiplexer #(.width(2)) multiplexer_5 (
    .in0(multiplexer_3_out), .in1(2'b01), .out(multiplexer_5_out), .sel(or_5_out));  // open: en
  or or_5 (or_5_out, LW, SW);
  Multiplexer #(.width(3)) multiplexer_6 (
    .in0(multiplexer_4_out), .in1(3'b001), .out(multiplexer_6_out), .sel(or_6_out));  // open: en
  or or_6 (or_6_out, SUB, BEQ);
  or or_7 (RegDst, ADD, SUB);
  or or_8 (ALUSrc, ORI, LW, LUI, SW);
  buf or_9 (MemToReg, LW);  // OR_Gate
  or or_10 (RegWrite, ADD, SUB, LUI, ORI, LW);
  buf or_11 (MemWrite, SW);  // OR_Gate
  buf or_12 (NEXT_PC_SEL, BEQ);  // OR_Gate
  Multiplexer #(.width(2)) multiplexer_7 (
    .in0(multiplexer_5_out), .in1(2'b00), .out(ExtOp), .sel(or_13_out));  // open: en
  buf or_13 (or_13_out, ORI);  // OR_Gate
  Multiplexer #(.width(3)) multiplexer_8 (
    .in0(multiplexer_6_out), .in1(3'b000), .out(ALUCtr), .sel(or_14_out));  // open: en
  or or_14 (or_14_out, ADD, SW, LW);
endmodule
