// Logisim project fibonacci_1.circ as structural Verilog: 3 circuits, main circuit main
module main (
  input  [2:0] in_1,
  output [3:0] out_2
);

  wire clock_1_out, not_1_out, \循环条件_1_out_3 ;
  wire [3:0] \循环体_1_out_3 ;

  Clock clock_1 (.out(clock_1_out));
  \循环条件  \u_循环条件_1  (.CLK(clock_1_out), .N(in_1), .out_3(\循环条件_1_out_3 ));
  Multiplexer #(.width(4)) multiplexer_1 (
    .in0(4'b0000), .in1(\循环体_1_out_3 ), .out(out_2), .sel(not_1_out));  // open: en
  \循环体  \u_循环体_1  (.ENA(\循环条件_1_out_3 ), .CLK(clock_1_out), .out_3(\循环体_1_out_3 ));
  not not_1 (not_1_out, \循环条件_1_out_3 );
endmodule

module \循环条件  (
  input  CLK,
  input  [2:0] N,
  output out_3
);

  wire comparator_1_eq, comparator_1_lt;
  wire [3:0] bit_extender_1_out, counter_1_q;

  Counter #(.width(4), .max('hf), .ongoal("stay")) counter_1 (
    .Q(counter_1_q), .clk(CLK));  // open: load, D, count, carry, clr
  assign bit_extender_1_out = {{1{1'b0}}, N};  // Bit_Extender bit_extender_1
  Comparator #(.width(4), .mode("unsigned")) comparator_1 (
    .a(counter_1_q), .b(bit_extender_1_out), .eq(comparator_1_eq), .lt(comparator_1_lt));  // open: gt
  or or_1 (out_3, comparator_1_eq, comparator_1_lt);
endmodule

module \循环体  (
  input  ENA,
  input  CLK,
  output [3:0] out_3
);

  wire counter_1_q;
  wire [3:0] adder_1_out, multiplexer_1_out, register_1_q;

  Multiplexer #(.width(4)) multiplexer_1 (
    .in0(4'b0001), .in1(out_3), .out(multiplexer_1_out), .sel(counter_1_q));  // open: en
  Counter #(.width(1), .max('h1), .ongoal("stay")) counter_1 (
    .Q(counter_1_q), .clk(CLK));  // open: load, D, count, carry, clr
  Adder #(.width(4)) adder_1 (.a(out_3), .b(register_1_q), .out(adder_1_out));  // open: cin, cout
  Register #(.width(4)) register_1 (.D(multiplexer_1_out), .en(ENA), .Q(register_1_q), .clk(CLK));  // open: clr
  Register #(.width(4)) register_2 (.D(adder_1_out), .en(ENA), .Q(out_3), .clk(CLK));  // open: clr
endmodule
