// Logisim project fibonacci_2.circ as structural Verilog: 9 circuits, main circuit main
module main (
  input  RST,
  input  [31:0] N,
  output [31:0] ANS_12
);

  wire clock_1_out, ena, \初始化条件_1_init ;
  wire [31:0] subtractor_1_out, \循环体_1_n_t , \循环体_1_out_11 , \循环体_1_out_21 , \循环体_1_out_22 ;

  Clock clock_1 (.out(clock_1_out));
  \初始化条件  \u_初始化条件_1  (.CLK(clock_1_out), .INIT(\初始化条件_1_init ));
  Subtractor #(.width(32)) subtractor_1 (.a(N), .b(32'h2), .out(subtractor_1_out));  // open: bin, bout
  // Probe on subtractor_1_out
  \循环体  \u_循环体_1  (
    .CLK(clock_1_out), .RST(RST), .INIT(\初始化条件_1_init ), .ENA(ena), .N_SUB_2(subtractor_1_out),
    .N_T(\循环体_1_n_t ), .OUT_11(\循环体_1_out_11 ), .OUT_12(ANS_12), .OUT_21(\循环体_1_out_21 ),
    .OUT_22(\循环体_1_out_22 ));
  \循环条件  \u_循环条件_1  (.N_NOW(\循环体_1_n_t ), .out_2(ena));
  // Probe on \循环体_1_out_11 
  // Probe on \循环体_1_out_21 
  // Probe on \循环体_1_out_22 
endmodule

module \_2_2矩阵寄存器  (
  input  [31:0] IN_11,
  input  [31:0] IN_12,
  input  [31:0] IN_21,
  input  [31:0] IN_22,
  input  CLK,
  input  RST,
  output [31:0] OUT_11,
  output [31:0] OUT_12,
  output [31:0] OUT_21,
  output [31:0] OUT_22
);

  Register #(.width(32)) register_1 (.D(IN_11), .Q(OUT_11), .clk(CLK), .clr(RST));  // open: en
  Register #(.width(32)) register_2 (.D(IN_12), .Q(OUT_12), .clk(CLK), .clr(RST));  // open: en
  Register #(.width(32)) register_3 (.D(IN_21), .Q(OUT_21), .clk(CLK), .clr(RST));  // open: en
  Register #(.width(32)) register_4 (.D(IN_22), .Q(OUT_22), .clk(CLK), .clr(RST));  // open: en
endmodule

module \_2_2矩阵乘法器  (
  input  [31:0] IN_A_11,
  input  [31:0] IN_A_12,
  input  [31:0] IN_A_21,
  input  [31:0] IN_A_22,
  input  [31:0] IN_B_11,
  input  [31:0] IN_B_12,
  input  [31:0] IN_B_21,
  input  [31:0] IN_B_22,
  output [31:0] OUT_11,
  output [31:0] OUT_12,
  output [31:0] OUT_21,
  output [31:0] OUT_22
);

  wire [31:0] multiplier_1_out, multiplier_2_out, multiplier_3_out, multiplier_4_out, multiplier_5_out,
       multiplier_6_out, multiplier_7_out, multiplier_8_out;

  Multiplier #(.width(32)) multiplier_1 (.a(IN_A_11), .b(IN_B_11), .out(multiplier_1_out));  // open: cin, cout
  Multiplier #(.width(32)) multiplier_2 (.a(IN_A_12), .b(IN_B_21), .out(multiplier_2_out));  // open: cin, cout
  Multiplier #(.width(32)) multiplier_3 (.a(IN_A_11), .b(IN_B_12), .out(multiplier_3_out));  // open: cin, cout
  Multiplier #(.width(32)) multiplier_4 (.a(IN_A_12), .b(IN_B_22), .out(multiplier_4_out));  // open: cin, cout
  Multiplier #(.width(32)) multiplier_5 (.a(IN_A_21), .b(IN_B_11), .out(multiplier_5_out));  // open: cin, cout
  Multiplier #(.width(32)) multiplier_6 (.a(IN_A_22), .b(IN_B_12), .out(multiplier_6_out));  // open: cin, cout
  Multiplier #(.width(32)) multiplier_7 (.a(IN_A_21), .b(IN_B_12), .out(multiplier_7_out));  // open: cin, cout
  Multiplier #(.width(32)) multiplier_8 (.a(IN_A_22), .b(IN_B_22), .out(multiplier_8_out));  // open: cin, cout
  Adder #(.width(32)) adder_1 (.a(multiplier_1_out), .b(multiplier_2_out), .out(OUT_11));  // open: cin, cout
  Adder #(.width(32)) adder_2 (.a(multiplier_3_out), .b(multiplier_4_out), .out(OUT_12));  // open: cin, cout
  Adder #(.width(32)) adder_3 (.a(multiplier_5_out), .b(multiplier_6_out), .out(OUT_21));  // open: cin, cout
  Adder #(.width(32)) adder_4 (.a(multiplier_7_out), .b(multiplier_8_out), .out(OUT_22));  // open: cin, cout
endmodule

module \_2_2矩阵MUX  (
  input  [31:0] IN_0_11,
  input  [31:0] IN_0_12,
  input  [31:0] IN_0_21,
  input  [31:0] IN_0_22,
  input  [31:0] IN_1_11,
  input  [31:0] IN_1_12,
  input  SEL,
  input  [31:0] IN_1_21,
  input  [31:0] IN_1_22,
  output [31:0] OUT_11,
  output [31:0] OUT_12,
  output [31:0] OUT_21,
  output [31:0] OUT_22
);

  Multiplexer #(.width(32)) multiplexer_1 (.in0(IN_0_11), .in1(IN_1_11), .out(OUT_11), .sel(SEL));  // open: en
  Multiplexer #(.width(32)) multiplexer_2 (.in0(IN_0_12), .in1(IN_1_12), .out(OUT_12), .sel(SEL));  // open: en
  Multiplexer #(.width(32)) multiplexer_3 (.in0(IN_0_21), .in1(IN_1_21), .out(OUT_21), .sel(SEL));  // open: en
  Multiplexer #(.width(32)) multiplexer_4 (.in0(IN_0_22), .in1(IN_1_22), .out(OUT_22), .sel(SEL));  // open: en
endmodule

module \Fib_初始值  (
  output [31:0] ORI_11,
  output [31:0] ORI_12,
  output [31:0] ORI_21,
  output [31:0] ORI_22
);


  assign ORI_11 = 32'h1;
  assign ORI_12 = 32'h1;
  assign ORI_21 = 32'h1;
  assign ORI_22 = {32{1'b0}};
endmodule

module \_2_2单位矩阵  (
  output [31:0] UNI_11,
  output [31:0] UNI_12,
  output [31:0] UNI_21,
  output [31:0] UNI_22
);


  assign UNI_11 = 32'h1;
  assign UNI_12 = 32'h1;
  assign UNI_21 = 32'h1;
  assign UNI_22 = 32'h1;
endmodule

module \循环条件  (
  input  [31:0] N_NOW,
  output out_2
);

  Comparator #(.width(32), .mode("unsigned")) comparator_1 (.a(N_NOW), .b({32{1'b0}}), .gt(out_2));  // open: eq, lt
endmodule

module \循环体  (
  input  CLK,
  input  RST,
  input  INIT,
  input  ENA,
  input  [31:0] N_SUB_2,
  output [31:0] N_T,
  output [31:0] OUT_11,
  output [31:0] OUT_12,
  output [31:0] OUT_21,
  output [31:0] OUT_22
);

  wire comparator_1_gt;
  wire [31:0] a_next_11, a_next_12, a_next_21, a_next_22, a_now_11, a_now_12, a_now_21, a_now_22, A_R_out_11,
       A_R_out_12, A_R_out_21, A_R_out_22, and_1_out, \fib_初始值_1_ori_11 , \fib_初始值_1_ori_12 ,
       \fib_初始值_1_ori_21 , \fib_初始值_1_ori_22 , \fib_初始值_2_ori_11 , \fib_初始值_2_ori_12 , \fib_初始值_2_ori_21 ,
       \fib_初始值_2_ori_22 , multiplexer_1_out, \n2_2单位矩阵_1_uni_11 , \n2_2单位矩阵_1_uni_12 , \n2_2单位矩阵_1_uni_21 ,
       \n2_2单位矩阵_1_uni_22 , \n2_2单位矩阵_2_uni_11 , \n2_2单位矩阵_2_uni_12 , \n2_2单位矩阵_2_uni_21 ,
       \n2_2单位矩阵_2_uni_22 , \n2_2矩阵mux_1_out_11 , \n2_2矩阵mux_1_out_12 , \n2_2矩阵mux_1_out_21 ,
       \n2_2矩阵mux_1_out_22 , \n2_2矩阵mux_2_out_11 , \n2_2矩阵mux_2_out_12 , \n2_2矩阵mux_2_out_21 ,
       \n2_2矩阵mux_2_out_22 , \n2_2矩阵mux_3_out_11 , \n2_2矩阵mux_3_out_12 , \n2_2矩阵mux_3_out_21 ,
       \n2_2矩阵mux_3_out_22 , n_next, N_R_q, s_next_11, s_next_12, s_next_21, s_next_22, s_now_11, s_now_12,
       s_now_21, s_now_22, S_R_out_11, S_R_out_12, S_R_out_21, S_R_out_22;

  Multiplexer #(.width(32)) multiplexer_1 (
    .in0(n_next), .in1(N_SUB_2), .out(multiplexer_1_out), .sel(INIT));  // open: en
  assign and_1_out = N_T & 32'h1;  // AND_Gate and_1, 32 bits wide
  // Probe on N_T
  // Probe on n_next
  Register #(.width(32)) N_R (.D(multiplexer_1_out), .Q(N_R_q), .clk(CLK), .clr(RST));  // open: en
  Multiplexer #(.width(32)) multiplexer_2 (.in0(N_R_q), .in1(N_SUB_2), .out(N_T), .sel(INIT));  // open: en
  \_2_2矩阵MUX  \u_2_2矩阵mux_1  (
    .IN_0_11(s_now_11), .IN_0_12(s_now_12), .IN_0_21(s_now_21), .IN_0_22(s_now_22), .IN_1_11(s_next_11),
    .IN_1_12(s_next_12), .IN_1_21(s_next_21), .IN_1_22(s_next_22), .SEL(comparator_1_gt),
    .OUT_11(\n2_2矩阵mux_1_out_11 ), .OUT_12(\n2_2矩阵mux_1_out_12 ), .OUT_21(\n2_2矩阵mux_1_out_21 ),
    .OUT_22(\n2_2矩阵mux_1_out_22 ));
  Comparator #(.width(32), .mode("unsigned")) comparator_1 (
    .a(and_1_out), .b({32{1'b0}}), .gt(comparator_1_gt));  // open: eq, lt
  Shifter #(.width(32), .shift("lr")) shifter_1 (.in(N_R_q), .\dist (5'b00001), .out(n_next));
  \_2_2单位矩阵  \u_2_2单位矩阵_1  (
    .UNI_11(\n2_2单位矩阵_1_uni_11 ), .UNI_12(\n2_2单位矩阵_1_uni_12 ), .UNI_21(\n2_2单位矩阵_1_uni_21 ),
    .UNI_22(\n2_2单位矩阵_1_uni_22 ));
  \Fib_初始值  \fib_初始值_1  (
    .ORI_11(\fib_初始值_1_ori_11 ), .ORI_12(\fib_初始值_1_ori_12 ), .ORI_21(\fib_初始值_1_ori_21 ),
    .ORI_22(\fib_初始值_1_ori_22 ));
  \_2_2矩阵寄存器  S_R (
    .IN_11(\n2_2矩阵mux_2_out_11 ), .IN_12(\n2_2矩阵mux_2_out_12 ), .IN_21(\n2_2矩阵mux_2_out_21 ),
    .IN_22(\n2_2矩阵mux_2_out_22 ), .CLK(CLK), .RST(RST), .OUT_11(S_R_out_11), .OUT_12(S_R_out_12),
    .OUT_21(S_R_out_21), .OUT_22(S_R_out_22));
  \_2_2矩阵MUX  \u_2_2矩阵mux_2  (
    .IN_0_11(\n2_2矩阵mux_1_out_11 ), .IN_0_12(\n2_2矩阵mux_1_out_12 ), .IN_0_21(\n2_2矩阵mux_1_out_21 ),
    .IN_0_22(\n2_2矩阵mux_1_out_22 ), .IN_1_11(\n2_2单位矩阵_1_uni_11 ), .IN_1_12(\n2_2单位矩阵_1_uni_12 ),
    .IN_1_21(\n2_2单位矩阵_1_uni_21 ), .IN_1_22(\n2_2单位矩阵_1_uni_22 ), .SEL(INIT), .OUT_11(\n2_2矩阵mux_2_out_11 ),
    .OUT_12(\n2_2矩阵mux_2_out_12 ), .OUT_21(\n2_2矩阵mux_2_out_21 ), .OUT_22(\n2_2矩阵mux_2_out_22 ));
  // Probe on a_now_11
  // Probe on a_now_21
  \_2_2矩阵MUX  \u_2_2矩阵mux_3  (
    .IN_0_11(a_next_11), .IN_0_12(a_next_12), .IN_0_21(a_next_21), .IN_0_22(a_next_22),
    .IN_1_11(\fib_初始值_1_ori_11 ), .IN_1_12(\fib_初始值_1_ori_12 ), .IN_1_21(\fib_初始值_1_ori_21 ),
    .IN_1_22(\fib_初始值_1_ori_22 ), .SEL(INIT), .OUT_11(\n2_2矩阵mux_3_out_11 ), .OUT_12(\n2_2矩阵mux_3_out_12 ),
    .OUT_21(\n2_2矩阵mux_3_out_21 ), .OUT_22(\n2_2矩阵mux_3_out_22 ));
  \_2_2单位矩阵  \u_2_2单位矩阵_2  (
    .UNI_11(\n2_2单位矩阵_2_uni_11 ), .UNI_12(\n2_2单位矩阵_2_uni_12 ), .UNI_21(\n2_2单位矩阵_2_uni_21 ),
    .UNI_22(\n2_2单位矩阵_2_uni_22 ));
  \_2_2矩阵寄存器  A_R (
    .IN_11(\n2_2矩阵mux_3_out_11 ), .IN_12(\n2_2矩阵mux_3_out_12 ), .IN_21(\n2_2矩阵mux_3_out_21 ),
    .IN_22(\n2_2矩阵mux_3_out_22 ), .CLK(CLK), .RST(RST), .OUT_11(A_R_out_11), .OUT_12(A_R_out_12),
    .OUT_21(A_R_out_21), .OUT_22(A_R_out_22));
  \_2_2矩阵MUX  \u_2_2矩阵mux_4  (
    .IN_0_11(S_R_out_11), .IN_0_12(S_R_out_12), .IN_0_21(S_R_out_21), .IN_0_22(S_R_out_22),
    .IN_1_11(\n2_2单位矩阵_2_uni_11 ), .IN_1_12(\n2_2单位矩阵_2_uni_12 ), .IN_1_21(\n2_2单位矩阵_2_uni_21 ),
    .IN_1_22(\n2_2单位矩阵_2_uni_22 ), .SEL(INIT), .OUT_11(s_now_11), .OUT_12(s_now_12), .OUT_21(s_now_21),
    .OUT_22(s_now_22));
  // Probe on a_now_12
  // Probe on a_now_22
  \_2_2矩阵MUX  \u_2_2矩阵mux_5  (
    .IN_0_11(A_R_out_11), .IN_0_12(A_R_out_12), .IN_0_21(A_R_out_21), .IN_0_22(A_R_out_22),
    .IN_1_11(\fib_初始值_2_ori_11 ), .IN_1_12(\fib_初始值_2_ori_12 ), .IN_1_21(\fib_初始值_2_ori_21 ),
    .IN_1_22(\fib_初始值_2_ori_22 ), .SEL(INIT), .OUT_11(a_now_11), .OUT_12(a_now_12), .OUT_21(a_now_21),
    .OUT_22(a_now_22));
  \Fib_初始值  \fib_初始值_2  (
    .ORI_11(\fib_初始值_2_ori_11 ), .ORI_12(\fib_初始值_2_ori_12 ), .ORI_21(\fib_初始值_2_ori_21 ),
    .ORI_22(\fib_初始值_2_ori_22 ));
  \_2_2矩阵乘法器  \u_2_2矩阵乘法器_1  (
    .IN_A_11(a_now_11), .IN_A_12(a_now_12), .IN_A_21(a_now_21), .IN_A_22(a_now_22), .IN_B_11(s_now_11),
    .IN_B_12(s_now_12), .IN_B_21(s_now_21), .IN_B_22(s_now_22), .OUT_11(s_next_11), .OUT_12(s_next_12),
    .OUT_21(s_next_21), .OUT_22(s_next_22));
  \_2_2矩阵乘法器  \u_2_2矩阵乘法器_2  (
    .IN_A_11(a_now_11), .IN_A_12(a_now_12), .IN_A_21(a_now_21), .IN_A_22(a_now_22), .IN_B_11(a_now_11),
    .IN_B_12(a_now_12), .IN_B_21(a_now_21), .IN_B_22(a_now_22), .OUT_11(a_next_11), .OUT_12(a_next_12),
    .OUT_21(a_next_21), .OUT_22(a_next_22));
  // Probe on s_next_11
  // Probe on s_next_12
  // Probe on s_now_11
  // Probe on s_now_21
  // Probe on s_now_12
  // Probe on s_now_22
  Multiplexer #(.width(32)) multiplexer_3 (.in0(s_now_11), .in1({32{1'b0}}), .out(OUT_11), .sel(ENA));  // open: en
  Multiplexer #(.width(32)) multiplexer_4 (.in0(s_now_12), .in1({32{1'b0}}), .out(OUT_12), .sel(ENA));  // open: en
  Multiplexer #(.width(32)) multiplexer_5 (.in0(s_now_21), .in1({32{1'b0}}), .out(OUT_21), .sel(ENA));  // open: en
  Multiplexer #(.width(32)) multiplexer_6 (.in0(s_now_22), .in1({32{1'b0}}), .out(OUT_22), .sel(ENA));  // open: en

  // Other names for the same wires on the sheet: n_now[31:0] = N_T
endmodule

module \初始化条件  (
  input  CLK,
  output INIT
);

  wire counter_1_q;

  Counter #(.width(1), .max('h1), .ongoal("stay")) counter_1 (
    .Q(counter_1_q), .clk(CLK));  // open: load, D, count, carry, clr
  not not_1 (INIT, counter_1_q);
endmodule
