// Logisim project D_Latch.circ as structural Verilog: 1 circuit, main circuit main
module main (
  input  CLK,
  input  D,
  output Q1,
  output Q2
);

  wire A1_out, A2_out, not_1_out;

  not not_1 (not_1_out, D);
  // Probe on not_1_out
  and A1 (A1_out, CLK, not_1_out);
  and A2 (A2_out, CLK, D);
  // Probe on A1_out
  // Probe on Q2
  // Probe on Q1
  // Probe on A2_out
  nor N1 (Q1, A1_out, Q2);
  nor N2 (Q2, Q1, A2_out);
endmodule
