// Logisim project D_Register.circ as structural Verilog: 1 circuit, main circuit main
module main (
  input  CLK,
  input  D,
  output Q1,
  output Q2
);

  wire and_1_out, and_2_out, and_3_out, and_4_out, nor_1_out, nor_2_out, not_1_out, not_2_out, not_3_out;

  not not_1 (not_1_out, CLK);
  not not_2 (not_2_out, D);
  and and_1 (and_1_out, not_1_out, not_2_out);
  and and_2 (and_2_out, not_1_out, D);
  nor nor_1 (nor_1_out, and_1_out, nor_2_out);
  nor nor_2 (nor_2_out, nor_1_out, and_2_out);
  not not_3 (not_3_out, nor_1_out);
  and and_3 (and_3_out, CLK, not_3_out);
  and and_4 (and_4_out, CLK, nor_1_out);
  nor nor_3 (Q1, and_3_out, Q2);
  nor nor_4 (Q2, Q1, and_4_out);
endmodule
