// Logisim project D_Register_EN.circ as structural Verilog: 1 circuit, main circuit main
module main (
  input  CLK,
  input  EN,
  input  D,
  output Q
);

  wire and_1_out, and_2_out, and_3_out, and_4_out, and_5_out, and_6_out, nor_1_out, nor_2_out, nor_4_out,
       not_1_out, not_2_out, not_3_out, not_4_out, or_1_out;

  and and_1 (and_1_out, Q, not_1_out);
  not not_1 (not_1_out, EN);
  and and_2 (and_2_out, EN, D);
  not not_2 (not_2_out, CLK);
  or or_1 (or_1_out, and_1_out, and_2_out);
  not not_3 (not_3_out, or_1_out);
  and and_3 (and_3_out, not_2_out, not_3_out);
  and and_4 (and_4_out, not_2_out, or_1_out);
  nor nor_1 (nor_1_out, and_3_out, nor_2_out);
  nor nor_2 (nor_2_out, nor_1_out, and_4_out);
  and and_5 (and_5_out, CLK, not_4_out);
  not not_4 (not_4_out, nor_1_out);
  and and_6 (and_6_out, CLK, nor_1_out);
  nor nor_3 (Q, and_5_out, nor_4_out);
  nor nor_4 (nor_4_out, Q, and_6_out);
endmodule
