// Logisim project RS_Latch.circ as structural Verilog: 1 circuit, main circuit main
module main (
  input  R,
  input  S,
  output Q1,
  output Q2
);

  // Probe on Q2
  // Probe on Q1
  nor N1 (Q1, R, Q2);
  nor N2 (Q2, Q1, S);
endmodule
